// Logisim project proj_2_2_top.circ as structural Verilog: 18 circuits, main circuit TOP
module TOP (
  input  clk,
  input  rst,
  input  [31:0] inst,
  output [31:0] current_pc_if,
  output mem_wen_mem,
  output [31:0] mem_din_mem,
  output [31:0] mem_dout_mem,
  output [31:0] mem_addr_mem,
  output control_en_mem,
  output [31:0] control_pc_mem,
  output wb_en_wb,
  output [4:0] wb_addr_wb,
  output [31:0] wb_data_wb
);

  wire alu_1_jump, Check_1, Check_2, Check_3, Check_4, control_en_mem_t, control_logic_stage4_1_wb_sel,
       Jump_stage3_q, Jump_stage4, mem_wen_mem_t, multiplexer_22_out, or_1_out, or_2_out, or_3_out, or_4_out,
       or_5_out, or_6_out, Read_half_stage4, RegWEn_stage5, WBstage, Write_half_stage4;
  wire [1:0] Hazard_A, Hazard_B;
  wire [3:0] inst_id_stage2, Inst_id_stage3, Inst_id_stage4;
  wire [4:0] Addr_A_stage2, Addr_B_stage2, Addr_D;
  wire [31:0] ALU_result_stage3, ALU_result_stage4, ALUResult_stage3_q, control_pc_mem_t, current_pc_if_t,
       Data_A_stage3, Data_A_stage_2_q, Data_B_stage3, Data_B_stage3_q, Data_B_stage4, Data_B_stage_2_q,
       dmem_1_data_output, IMM_stage3, Inst_stage_1_q, Inst_stage_2_q, Inst_stage_3_q, Inst_stage_4_q,
       Inst_stage_transfer_1to2, Inst_stage_transfer_2to3, Inst_stage_transfer_3to4,
       Inst_stage_transfer_4to5, mem_dout_mem_t, multiplexer_12_out, multiplexer_13_out, multiplexer_14_out,
       multiplexer_15_out, multiplexer_16_out, multiplexer_17_out, multiplexer_21_out, multiplexer_23_out,
       multiplexer_24_out, multiplexer_25_out, New_PC, New_PC_addr_stage4, Pc_stage_transfer_1to2,
       Pc_stage_transfer_2to3, reg_set_1_dataa, reg_set_1_datab, wb_data_wb_t, Write_back_data;

  PC_circuit pc_circuit_1 (
    .pc_value(New_PC_addr_stage4), .control_en(control_en_mem_t), .clk(clk), .rst(rst),
    .inst_addr(current_pc_if_t), .control_pc(control_pc_mem_t));
  Register #(.width(32)) Inst_stage_1 (.D(inst), .clk(clk), .Q(Inst_stage_1_q), .clr(rst));  // open: en
  Register #(.width(32)) PC_stage_1 (
    .D(current_pc_if_t), .clk(clk), .Q(Pc_stage_transfer_1to2), .clr(rst));  // open: en
  Multiplexer #(.width(32)) multiplexer_1 (
    .in0(Inst_stage_1_q), .in1({32{1'b0}}),
    .out({Inst_stage_transfer_1to2[31:25], Addr_B_stage2, Addr_A_stage2, Inst_stage_transfer_1to2[14:0]}),
    .sel(Check_1));
  Comparator #(.width(32)) comparator_1 (.a(Inst_stage_1_q), .b({32{1'b0}}), .eq(Check_1));  // open: gt, lt
  Multiplexer #(.width(32)) multiplexer_2 (.in0(current_pc_if_t), .in1({32{1'b0}}), .out(current_pc_if), .sel(rst));
  Multiplexer multiplexer_3 (.in0(mem_wen_mem_t), .in1(1'b0), .out(mem_wen_mem), .sel(or_1_out));
  or or_1 (or_1_out, rst, Check_3);
  Multiplexer #(.width(32)) multiplexer_4 (.in0(Data_B_stage4), .in1({32{1'b0}}), .out(mem_din_mem), .sel(or_2_out));
  or or_2 (or_2_out, rst, Check_3);
  Multiplexer #(.width(32)) multiplexer_5 (.in0(mem_dout_mem_t), .in1({32{1'b0}}), .out(mem_dout_mem), .sel(or_3_out));
  or or_3 (or_3_out, rst, Check_3);
  Multiplexer #(.width(32)) multiplexer_6 (
    .in0(ALU_result_stage4), .in1({32{1'b0}}), .out(mem_addr_mem), .sel(or_6_out));
  Multiplexer multiplexer_7 (.in0(control_en_mem_t), .in1(1'b0), .out(control_en_mem), .sel(or_4_out));
  or or_4 (or_4_out, rst, Check_3);
  Multiplexer #(.width(32)) multiplexer_8 (
    .in0(control_pc_mem_t), .in1({32{1'b0}}), .out(control_pc_mem), .sel(or_5_out));
  or or_5 (or_5_out, rst, Check_3);
  Multiplexer multiplexer_9 (.in0(RegWEn_stage5), .in1(1'b0), .out(wb_en_wb), .sel(WBstage));
  Multiplexer #(.width(5)) multiplexer_10 (.in0(Addr_D), .in1({5{1'b0}}), .out(wb_addr_wb), .sel(WBstage));
  Multiplexer #(.width(32)) multiplexer_11 (.in0(wb_data_wb_t), .in1({32{1'b0}}), .out(wb_data_wb), .sel(WBstage));
  or or_6 (or_6_out, rst, Check_3);
  Reg_set reg_set_1 (
    .AddrD(Addr_D), .DataD(wb_data_wb_t), .AddrA(Addr_A_stage2), .AddrB(Addr_B_stage2),
    .RegWEn(RegWEn_stage5), .rst(rst), .clk(clk), .DataA(reg_set_1_dataa), .DataB(reg_set_1_datab));
  Data_Hazard_logic_B data_hazard_logic_b_1 (
    .Inst_now({Inst_stage_transfer_1to2[31:25], Addr_B_stage2, Addr_A_stage2, Inst_stage_transfer_1to2[14:0]}),
    .Inst_id_now(inst_id_stage2), .Inst_last_1(Inst_stage_transfer_2to3), .Inst_id_last_1(Inst_id_stage3),
    .Inst_last_2(Inst_stage_transfer_3to4), .Inst_id_last_2(Inst_id_stage4), .Data_Hazard_choice(Hazard_B));
  Data_Hazard_logic_A data_hazard_logic_a_1 (
    .Inst_now({Inst_stage_transfer_1to2[31:25], Addr_B_stage2, Addr_A_stage2, Inst_stage_transfer_1to2[14:0]}),
    .Inst_id_now(inst_id_stage2), .Inst_last_1(Inst_stage_transfer_2to3), .Inst_id_last_1(Inst_id_stage3),
    .Inst_last_2(Inst_stage_transfer_3to4), .Inst_id_last_2(Inst_id_stage4), .Data_Hazard_choice(Hazard_A));
  or or_7 (WBstage, rst, Check_4);
  Control_logic_stage2 control_logic_stage2_1 (
    .Inst({Inst_stage_transfer_1to2[31:25], Addr_B_stage2, Addr_A_stage2, Inst_stage_transfer_1to2[14:0]}),
    .inst_id(inst_id_stage2));
  Multiplexer #(.select(2), .width(32)) multiplexer_12 (
    .in0(reg_set_1_dataa), .in1(ALU_result_stage3), .in2(Write_back_data), .out(multiplexer_12_out),
    .sel(Hazard_A));  // open: in3
  Multiplexer #(.select(2), .width(32)) multiplexer_13 (
    .in0(reg_set_1_datab), .in1(ALU_result_stage3), .in2(Write_back_data), .out(multiplexer_13_out),
    .sel(Hazard_B));  // open: in3
  Multiplexer #(.width(32)) multiplexer_14 (
    .in0({Inst_stage_transfer_1to2[31:25], Addr_B_stage2, Addr_A_stage2, Inst_stage_transfer_1to2[14:0]}),
    .in1(32'h13), .out(multiplexer_14_out), .sel(control_en_mem_t));
  Multiplexer #(.width(32)) multiplexer_15 (
    .in0(multiplexer_12_out), .in1({32{1'b0}}), .out(multiplexer_15_out), .sel(control_en_mem_t));
  Multiplexer #(.width(32)) multiplexer_16 (
    .in0(multiplexer_13_out), .in1({32{1'b0}}), .out(multiplexer_16_out), .sel(control_en_mem_t));
  Register #(.width(32)) Inst_stage_2 (.D(multiplexer_14_out), .clk(clk), .Q(Inst_stage_2_q), .clr(rst));  // open: en
  Register #(.width(32)) Data_A_stage_2 (
    .D(multiplexer_15_out), .clk(clk), .Q(Data_A_stage_2_q), .clr(rst));  // open: en
  Register #(.width(32)) Data_B_stage_2 (
    .D(multiplexer_16_out), .clk(clk), .Q(Data_B_stage_2_q), .clr(rst));  // open: en
  Register #(.width(32)) PC_stage_2 (
    .D(multiplexer_17_out), .clk(clk), .Q(Pc_stage_transfer_2to3), .clr(rst));  // open: en
  Multiplexer #(.width(32)) multiplexer_17 (
    .in0(Pc_stage_transfer_1to2), .in1({32{1'b0}}), .out(multiplexer_17_out), .sel(control_en_mem_t));
  Multiplexer #(.width(32)) multiplexer_18 (
    .in0(Inst_stage_2_q), .in1({32{1'b0}}), .out(Inst_stage_transfer_2to3), .sel(Check_2));
  Comparator #(.width(32)) comparator_2 (.a(Inst_stage_2_q), .b({32{1'b0}}), .eq(Check_2));  // open: gt, lt
  Multiplexer #(.width(32)) multiplexer_19 (
    .in0(Data_A_stage_2_q), .in1({32{1'b0}}), .out(Data_A_stage3), .sel(Check_2));
  Multiplexer #(.width(32)) multiplexer_20 (
    .in0(Data_B_stage_2_q), .in1({32{1'b0}}), .out(Data_B_stage3), .sel(Check_2));
  Imm_Gen imm_gen_1 (.Inst(Inst_stage_transfer_2to3), .IMM_generate(IMM_stage3));
  Control_logic_stage3 control_logic_stage3_1 (.Inst(Inst_stage_transfer_2to3), .inst_id(Inst_id_stage3));
  ALU alu_1 (
    .Inst_id(Inst_id_stage3), .Current_pc(Pc_stage_transfer_2to3), .Data_A(Data_A_stage3),
    .Data_B(Data_B_stage3), .IMM(IMM_stage3), .ALU_OUT(ALU_result_stage3), .NEW_PC(New_PC), .Jump(alu_1_jump));
  Multiplexer #(.width(32)) multiplexer_21 (
    .in0(Inst_stage_transfer_2to3), .in1(32'h13), .out(multiplexer_21_out), .sel(control_en_mem_t));
  Multiplexer multiplexer_22 (.in0(alu_1_jump), .in1(1'b0), .out(multiplexer_22_out), .sel(control_en_mem_t));
  Register #(.width(32)) Inst_stage_3 (.D(multiplexer_21_out), .clk(clk), .Q(Inst_stage_3_q), .clr(rst));  // open: en
  Multiplexer #(.width(32)) multiplexer_23 (
    .in0(Data_B_stage3), .in1({32{1'b0}}), .out(multiplexer_23_out), .sel(control_en_mem_t));
  Multiplexer #(.width(32)) multiplexer_24 (
    .in0(ALU_result_stage3), .in1({32{1'b0}}), .out(multiplexer_24_out), .sel(control_en_mem_t));
  Multiplexer #(.width(32)) multiplexer_25 (
    .in0(New_PC), .in1({32{1'b0}}), .out(multiplexer_25_out), .sel(control_en_mem_t));
  Register #(.width(32)) u_Data_B_stage3 (
    .D(multiplexer_23_out), .clk(clk), .Q(Data_B_stage3_q), .clr(rst));  // open: en
  Register #(.width(1)) Jump_stage3 (.D(multiplexer_22_out), .clk(clk), .Q(Jump_stage3_q), .clr(rst));  // open: en
  Register #(.width(32)) ALUResult_stage3 (
    .D(multiplexer_24_out), .clk(clk), .Q(ALUResult_stage3_q), .clr(rst));  // open: en
  Register #(.width(32)) PC_stage_3 (.D(multiplexer_25_out), .clk(clk), .Q(New_PC_addr_stage4), .clr(rst));  // open: en
  Multiplexer #(.width(32)) multiplexer_26 (
    .in0(Inst_stage_3_q), .in1({32{1'b0}}), .out(Inst_stage_transfer_3to4), .sel(Check_3));
  Comparator #(.width(32)) comparator_3 (.a(Inst_stage_3_q), .b({32{1'b0}}), .eq(Check_3));  // open: gt, lt
  Multiplexer #(.width(32)) multiplexer_27 (
    .in0(Data_B_stage3_q), .in1({32{1'b0}}), .out(Data_B_stage4), .sel(Check_3));
  Multiplexer multiplexer_28 (.in0(Jump_stage3_q), .in1(1'b0), .out(Jump_stage4), .sel(Check_3));
  Multiplexer #(.width(32)) multiplexer_29 (
    .in0(ALUResult_stage3_q), .in1({32{1'b0}}), .out(ALU_result_stage4), .sel(Check_3));
  Control_logic_stage4 control_logic_stage4_1 (
    .Inst(Inst_stage_transfer_3to4), .inst_id(Inst_id_stage4), .WB_sel(control_logic_stage4_1_wb_sel),
    .MemRW(mem_wen_mem_t), .Write_half(Write_half_stage4), .Read_half(Read_half_stage4));
  DMEM dmem_1 (
    .rst(rst), .Write_half(Write_half_stage4), .Read_half(Read_half_stage4), .Addr(ALU_result_stage4),
    .data_D(Data_B_stage4), .MemRW(mem_wen_mem_t), .clk(clk), .DATA_output(dmem_1_data_output));
  Control_Hazard_logic control_hazard_logic_1 (.Jump(Jump_stage4), .Control_Hazard(control_en_mem_t));
  Multiplexer #(.width(32)) multiplexer_30 (
    .in0(dmem_1_data_output), .in1({32{1'b0}}), .out(mem_dout_mem_t), .sel(mem_wen_mem_t));
  Multiplexer #(.width(32)) multiplexer_31 (
    .in0(mem_dout_mem_t), .in1(ALU_result_stage4), .out(Write_back_data), .sel(control_logic_stage4_1_wb_sel));
  Register #(.width(32)) Inst_stage_4 (
    .D(Inst_stage_transfer_3to4), .clk(clk), .Q(Inst_stage_4_q), .clr(rst));  // open: en
  Register #(.width(32)) Write_back_data_stage_4 (
    .D(Write_back_data), .clk(clk), .Q(wb_data_wb_t), .clr(rst));  // open: en
  Multiplexer #(.width(32)) multiplexer_32 (
    .in0(Inst_stage_4_q), .in1({32{1'b0}}),
    .out({Inst_stage_transfer_4to5[31:12], Addr_D, Inst_stage_transfer_4to5[6:0]}), .sel(Check_4));
  Comparator #(.width(32)) comparator_4 (.a(Inst_stage_4_q), .b({32{1'b0}}), .eq(Check_4));  // open: gt, lt
  Control_logic_stage5 control_logic_stage5_1 (
    .Inst({Inst_stage_transfer_4to5[31:12], Addr_D, Inst_stage_transfer_4to5[6:0]}), .RegWEn(RegWEn_stage5));  // open: inst_id

  // Other names for the same wires on the sheet: Control_Hazard_label = control_en_mem_t;
  //   inst_addr_stage1[31:0] = current_pc_if_t; Inst_stage_transfer_1to2[24:15] = {Addr_B_stage2, Addr_A_stage2};
  //   Inst_stage_transfer_4to5[11:7] = Addr_D; wb_addr_wb_t[4:0] = Addr_D; mem_addr_mem_t[31:0] = ALU_result_stage4;
  //   mem_din_mem_t[31:0] = Data_B_stage4; MemRW_stage4 = mem_wen_mem_t;
  //   Pc_stage_transfer_3to4[31:0] = New_PC_addr_stage4; WriteBackData_stage_5[31:0] = wb_data_wb_t;
  //   wb_en_wb_t = RegWEn_stage5

  // Notes on the sheet:
  //   Stage 1
  //   DON'T TOUCH!
  //   MEM stage output
  //   IF stage output
  //   WB stage output
  //   Stage 2
  //   Stage 3
  //   Stage 4
  //   Stage 5
endmodule

module testbench (
  input  rst,
  output [7:0] out_2,
  output [31:0] current_pc_if,
  output mem_wen_mem,
  output halt,
  output [31:0] mem_din_mem,
  output [31:0] mem_dout_mem,
  output [31:0] mem_addr_mem,
  output control_en_mem,
  output [31:0] control_pc_mem,
  output wb_en_wb,
  output [4:0] wb_addr_wb,
  output [31:0] wb_data_wb
);

  wire and_1_out, carry, clk, mem_wen_men, not_1_out, not_2_out, por_1_out, rst_t;
  wire [31:0] inst;

  not not_1 (not_1_out, inst[2]);
  not not_2 (not_2_out, inst[3]);
  POR por_1 (.out(por_1_out));
  TOP top_1 (
    .clk(clk), .rst(rst_t), .inst(inst), .current_pc_if(current_pc_if), .mem_wen_mem(mem_wen_men),
    .mem_din_mem(mem_din_mem), .mem_dout_mem(mem_dout_mem), .mem_addr_mem(mem_addr_mem),
    .control_en_mem(control_en_mem), .control_pc_mem(control_pc_mem), .wb_en_wb(wb_en_wb),
    .wb_addr_wb(wb_addr_wb), .wb_data_wb(wb_data_wb));
  Clock clock_1 (.out(clk));
  or or_1 (rst_t, rst, por_1_out);
  and and_1 (and_1_out, inst[0], inst[1], not_1_out, not_2_out, inst[4], inst[5], inst[6]);
  or or_2 (halt, and_1_out, carry);
  Counter counter_1 (.clr(rst_t), .up(1'b1), .count(1'b1), .clk(clk), .carry(carry), .Q(out_2));  // open: load, D
  // ROM #(.line("quad"), .misaligned("true")) rom_1: pin names not known; wires that end beside it: current_pc_if[7:0], inst[7:0], inst[15:8], inst[23:16], inst[31:24]
  // Probe on inst

  // Notes on the sheet:
  //   DON'T TOUCH!
  //   contents of rom_1 (hex, n*v repeats v):
  //   b7 60 87 f9 13 1 90 1 93 1 a0 1 33 d2 10 40 b3 d2 20 40 33 d3 30 40 93 3 80 fe 33 4 32 0 b3 a4 21 0
  //   23 28 10 2 23 1a 10 2 3 25 0 3 23 1a b0 2 13 f6 c2 ab 93 b6 10 c3 13 d7 23 0 97 77 f8 ff 13 0 0 0 13
  //   0 0 0 13 0 0 0 13 0 0 0 73 0 10
  //   IF stage output
  //   MEM stage output
  //   WB stage output
  //   test
endmodule

module PC_circuit (
  input  [31:0] pc_value,
  input  control_en,
  input  clk,
  input  rst,
  output [31:0] inst_addr,
  output [31:0] control_pc
);

  wire [31:0] adder_1_out, multiplexer_1_out;

  Multiplexer #(.width(32)) multiplexer_1 (
    .in0(adder_1_out), .in1(pc_value), .out(multiplexer_1_out), .sel(control_en));
  Register #(.width(32)) pc (.D(control_pc), .clk(clk), .Q(inst_addr), .clr(rst));  // open: en
  Address_aligned address_aligned_1 (.unaligned_address(multiplexer_1_out), .aligned_address(control_pc));
  Adder #(.width(32)) adder_1 (.a(32'h4), .b(inst_addr), .out(adder_1_out));  // open: cin, cout

  // Other names for the same wires on the sheet: PCSEL = control_en
endmodule

module Address_aligned (
  input  [31:0] unaligned_address,
  output [31:0] aligned_address
);

  wire [31:0] shifter_1_out, shifter_2_out;

  Shifter #(.shift("lr"), .width(32)) shifter_1 (.in(unaligned_address), .\dist (5'b00001), .out(shifter_1_out));
  Shifter #(.width(32)) shifter_2 (.in(shifter_1_out), .\dist (5'b00001), .out(shifter_2_out));
  assign aligned_address = {{24{1'b0}}, shifter_2_out[7:0]};  // Bit_Extender bit_extender_1
endmodule

module Reg_set (
  input  [4:0] AddrD,
  input  [31:0] DataD,
  input  [4:0] AddrA,
  input  [4:0] AddrB,
  input  RegWEn,
  input  rst,
  input  clk,
  output [31:0] DataA,
  output [31:0] DataB
);

  wire [31:0] Data_Reg_0, Data_Reg_1, Data_Reg_2, Data_Reg_3, Data_Reg_4, Data_Reg_5, Data_Reg_6, Data_Reg_7,
       Data_Reg_8, Data_Reg_9, Data_Reg_10, Data_Reg_11, Data_Reg_12, Data_Reg_13, Data_Reg_14, Data_Reg_15,
       Data_Reg_16, Data_Reg_17, Data_Reg_18, Data_Reg_19, Data_Reg_20, Data_Reg_21, Data_Reg_22,
       Data_Reg_23, Data_Reg_24, Data_Reg_25, Data_Reg_26, Data_Reg_27, Data_Reg_28, Data_Reg_29,
       Data_Reg_30, Data_Reg_31;

  Reg_with_compare_Reg0 reg_with_compare_reg0_1 (
    .AddrD(AddrD), .Reg_Addr({5{1'b0}}), .DataD(DataD), .clk(clk), .rst(rst), .RegWEn(RegWEn),
    .Current_data(Data_Reg_0));
  Reg_with_compare reg_with_compare_1 (
    .AddrD(AddrD), .Reg_Addr(5'b00100), .DataD(DataD), .clk(clk), .rst(rst), .RegWEn(RegWEn),
    .Current_data(Data_Reg_4));
  Reg_with_compare reg_with_compare_2 (
    .AddrD(AddrD), .Reg_Addr(5'b01000), .DataD(DataD), .clk(clk), .rst(rst), .RegWEn(RegWEn),
    .Current_data(Data_Reg_8));
  Reg_with_compare reg_with_compare_3 (
    .AddrD(AddrD), .Reg_Addr(5'b01100), .DataD(DataD), .clk(clk), .rst(rst), .RegWEn(RegWEn),
    .Current_data(Data_Reg_12));
  Reg_with_compare reg_with_compare_4 (
    .AddrD(AddrD), .Reg_Addr(5'b10000), .DataD(DataD), .clk(clk), .rst(rst), .RegWEn(RegWEn),
    .Current_data(Data_Reg_16));
  Reg_with_compare reg_with_compare_5 (
    .AddrD(AddrD), .Reg_Addr(5'b10100), .DataD(DataD), .clk(clk), .rst(rst), .RegWEn(RegWEn),
    .Current_data(Data_Reg_20));
  Reg_with_compare reg_with_compare_6 (
    .AddrD(AddrD), .Reg_Addr(5'b11000), .DataD(DataD), .clk(clk), .rst(rst), .RegWEn(RegWEn),
    .Current_data(Data_Reg_24));
  Reg_with_compare reg_with_compare_7 (
    .AddrD(AddrD), .Reg_Addr(5'b11100), .DataD(DataD), .clk(clk), .rst(rst), .RegWEn(RegWEn),
    .Current_data(Data_Reg_28));
  Multiplexer #(.select(5), .width(32)) multiplexer_1 (
    .in0(Data_Reg_0), .in1(Data_Reg_1), .in2(Data_Reg_2), .in3(Data_Reg_3), .in4(Data_Reg_4),
    .in5(Data_Reg_5), .in6(Data_Reg_6), .in7(Data_Reg_7), .in8(Data_Reg_8), .in9(Data_Reg_9),
    .in10(Data_Reg_10), .in11(Data_Reg_11), .in12(Data_Reg_12), .in13(Data_Reg_13), .in14(Data_Reg_14),
    .in15(Data_Reg_15), .in16(Data_Reg_16), .in17(Data_Reg_17), .in18(Data_Reg_18), .in19(Data_Reg_19),
    .in20(Data_Reg_20), .in21(Data_Reg_21), .in22(Data_Reg_22), .in23(Data_Reg_23), .in24(Data_Reg_24),
    .in25(Data_Reg_25), .in26(Data_Reg_26), .in27(Data_Reg_27), .in28(Data_Reg_28), .in29(Data_Reg_29),
    .in30(Data_Reg_30), .in31(Data_Reg_31), .out(DataA), .sel(AddrA));
  Reg_with_compare reg_with_compare_8 (
    .AddrD(AddrD), .Reg_Addr(5'b00001), .DataD(DataD), .clk(clk), .rst(rst), .RegWEn(RegWEn),
    .Current_data(Data_Reg_1));
  Reg_with_compare reg_with_compare_9 (
    .AddrD(AddrD), .Reg_Addr(5'b00101), .DataD(DataD), .clk(clk), .rst(rst), .RegWEn(RegWEn),
    .Current_data(Data_Reg_5));
  Reg_with_compare reg_with_compare_10 (
    .AddrD(AddrD), .Reg_Addr(5'b01001), .DataD(DataD), .clk(clk), .rst(rst), .RegWEn(RegWEn),
    .Current_data(Data_Reg_9));
  Reg_with_compare reg_with_compare_11 (
    .AddrD(AddrD), .Reg_Addr(5'b01101), .DataD(DataD), .clk(clk), .rst(rst), .RegWEn(RegWEn),
    .Current_data(Data_Reg_13));
  Reg_with_compare reg_with_compare_12 (
    .AddrD(AddrD), .Reg_Addr(5'b10001), .DataD(DataD), .clk(clk), .rst(rst), .RegWEn(RegWEn),
    .Current_data(Data_Reg_17));
  Reg_with_compare reg_with_compare_13 (
    .AddrD(AddrD), .Reg_Addr(5'b10101), .DataD(DataD), .clk(clk), .rst(rst), .RegWEn(RegWEn),
    .Current_data(Data_Reg_21));
  Reg_with_compare reg_with_compare_14 (
    .AddrD(AddrD), .Reg_Addr(5'b11001), .DataD(DataD), .clk(clk), .rst(rst), .RegWEn(RegWEn),
    .Current_data(Data_Reg_25));
  Reg_with_compare reg_with_compare_15 (
    .AddrD(AddrD), .Reg_Addr(5'b11101), .DataD(DataD), .clk(clk), .rst(rst), .RegWEn(RegWEn),
    .Current_data(Data_Reg_29));
  Reg_with_compare reg_with_compare_16 (
    .AddrD(AddrD), .Reg_Addr(5'b00010), .DataD(DataD), .clk(clk), .rst(rst), .RegWEn(RegWEn),
    .Current_data(Data_Reg_2));
  Reg_with_compare reg_with_compare_17 (
    .AddrD(AddrD), .Reg_Addr(5'b00110), .DataD(DataD), .clk(clk), .rst(rst), .RegWEn(RegWEn),
    .Current_data(Data_Reg_6));
  Reg_with_compare reg_with_compare_18 (
    .AddrD(AddrD), .Reg_Addr(5'b01010), .DataD(DataD), .clk(clk), .rst(rst), .RegWEn(RegWEn),
    .Current_data(Data_Reg_10));
  Reg_with_compare reg_with_compare_19 (
    .AddrD(AddrD), .Reg_Addr(5'b01110), .DataD(DataD), .clk(clk), .rst(rst), .RegWEn(RegWEn),
    .Current_data(Data_Reg_14));
  Reg_with_compare reg_with_compare_20 (
    .AddrD(AddrD), .Reg_Addr(5'b10010), .DataD(DataD), .clk(clk), .rst(rst), .RegWEn(RegWEn),
    .Current_data(Data_Reg_18));
  Reg_with_compare reg_with_compare_21 (
    .AddrD(AddrD), .Reg_Addr(5'b10110), .DataD(DataD), .clk(clk), .rst(rst), .RegWEn(RegWEn),
    .Current_data(Data_Reg_22));
  Reg_with_compare reg_with_compare_22 (
    .AddrD(AddrD), .Reg_Addr(5'b11010), .DataD(DataD), .clk(clk), .rst(rst), .RegWEn(RegWEn),
    .Current_data(Data_Reg_26));
  Reg_with_compare reg_with_compare_23 (
    .AddrD(AddrD), .Reg_Addr(5'b11110), .DataD(DataD), .clk(clk), .rst(rst), .RegWEn(RegWEn),
    .Current_data(Data_Reg_30));
  Multiplexer #(.select(5), .width(32)) multiplexer_2 (
    .in0(Data_Reg_0), .in1(Data_Reg_1), .in2(Data_Reg_2), .in3(Data_Reg_3), .in4(Data_Reg_4),
    .in5(Data_Reg_5), .in6(Data_Reg_6), .in7(Data_Reg_7), .in8(Data_Reg_8), .in9(Data_Reg_9),
    .in10(Data_Reg_10), .in11(Data_Reg_11), .in12(Data_Reg_12), .in13(Data_Reg_13), .in14(Data_Reg_14),
    .in15(Data_Reg_15), .in16(Data_Reg_16), .in17(Data_Reg_17), .in18(Data_Reg_18), .in19(Data_Reg_19),
    .in20(Data_Reg_20), .in21(Data_Reg_21), .in22(Data_Reg_22), .in23(Data_Reg_23), .in24(Data_Reg_24),
    .in25(Data_Reg_25), .in26(Data_Reg_26), .in27(Data_Reg_27), .in28(Data_Reg_28), .in29(Data_Reg_29),
    .in30(Data_Reg_30), .in31(Data_Reg_31), .out(DataB), .sel(AddrB));
  Reg_with_compare reg_with_compare_24 (
    .AddrD(AddrD), .Reg_Addr(5'b00011), .DataD(DataD), .clk(clk), .rst(rst), .RegWEn(RegWEn),
    .Current_data(Data_Reg_3));
  Reg_with_compare reg_with_compare_25 (
    .AddrD(AddrD), .Reg_Addr(5'b00111), .DataD(DataD), .clk(clk), .rst(rst), .RegWEn(RegWEn),
    .Current_data(Data_Reg_7));
  Reg_with_compare reg_with_compare_26 (
    .AddrD(AddrD), .Reg_Addr(5'b01011), .DataD(DataD), .clk(clk), .rst(rst), .RegWEn(RegWEn),
    .Current_data(Data_Reg_11));
  Reg_with_compare reg_with_compare_27 (
    .AddrD(AddrD), .Reg_Addr(5'b01111), .DataD(DataD), .clk(clk), .rst(rst), .RegWEn(RegWEn),
    .Current_data(Data_Reg_15));
  Reg_with_compare reg_with_compare_28 (
    .AddrD(AddrD), .Reg_Addr(5'b10011), .DataD(DataD), .clk(clk), .rst(rst), .RegWEn(RegWEn),
    .Current_data(Data_Reg_19));
  Reg_with_compare reg_with_compare_29 (
    .AddrD(AddrD), .Reg_Addr(5'b10111), .DataD(DataD), .clk(clk), .rst(rst), .RegWEn(RegWEn),
    .Current_data(Data_Reg_23));
  Reg_with_compare reg_with_compare_30 (
    .AddrD(AddrD), .Reg_Addr(5'b11011), .DataD(DataD), .clk(clk), .rst(rst), .RegWEn(RegWEn),
    .Current_data(Data_Reg_27));
  Reg_with_compare reg_with_compare_31 (
    .AddrD(AddrD), .Reg_Addr({5{1'b1}}), .DataD(DataD), .clk(clk), .rst(rst), .RegWEn(RegWEn),
    .Current_data(Data_Reg_31));

  // Notes on the sheet:
  //   8*4  input: addrd addra addrb datad clk regwen output: dataa datab
endmodule

module Reg_with_compare (
  input  [4:0] AddrD,
  input  [4:0] Reg_Addr,
  input  [31:0] DataD,
  input  clk,
  input  rst,
  input  RegWEn,
  output [31:0] Current_data
);

  wire and_1_out, comparator_1_eq;
  wire [31:0] multiplexer_1_out;

  Multiplexer #(.width(32)) multiplexer_1 (.in0(Current_data), .in1(DataD), .out(multiplexer_1_out), .sel(and_1_out));
  and and_1 (and_1_out, RegWEn, comparator_1_eq);
  Comparator #(.mode("unsigned"), .width(5)) comparator_1 (
    .a(Reg_Addr), .b(AddrD), .eq(comparator_1_eq));  // open: gt, lt
  Register #(.trigger("falling"), .width(32)) register_1 (
    .D(multiplexer_1_out), .clk(clk), .Q(Current_data), .clr(rst));  // open: en
endmodule

module Reg_with_compare_Reg0 (
  input  [4:0] AddrD,
  input  [4:0] Reg_Addr,
  input  [31:0] DataD,
  input  clk,
  input  rst,
  input  RegWEn,
  output [31:0] Current_data
);

  wire [31:0] multiplexer_1_out;

  Multiplexer #(.width(32)) multiplexer_1 (.in0(Current_data), .in1({32{1'b0}}), .out(multiplexer_1_out), .sel(1'b1));
  Register #(.trigger("falling"), .width(32)) register_1 (
    .D(multiplexer_1_out), .clk(clk), .Q(Current_data), .clr(rst));  // open: en
endmodule

module Imm_Gen (
  input  [31:0] Inst,
  output [31:0] IMM_generate
);

  wire comparator_1_eq, comparator_2_eq, comparator_3_eq, comparator_4_eq, comparator_5_eq, comparator_6_eq,
       comparator_7_eq, comparator_8_eq, comparator_9_eq, or_1_out, or_2_out;
  wire [31:0] B_type, bit_extender_1_out, bit_extender_2_out, bit_extender_3_out, bit_extender_4_out,
       bit_extender_5_out, I_type, J_type, R_type, S_type, shifter_1_out, shifter_2_out, U_type;

  Comparator #(.mode("unsigned"), .width(7)) comparator_1 (
    .a(Inst[6:0]), .b(7'b0000011), .eq(comparator_1_eq));  // open: gt, lt
  Comparator #(.mode("unsigned"), .width(7)) comparator_2 (
    .a(Inst[6:0]), .b(7'b0010011), .eq(comparator_2_eq));  // open: gt, lt
  Comparator #(.mode("unsigned"), .width(7)) comparator_3 (
    .a(Inst[6:0]), .b(7'b1100111), .eq(comparator_3_eq));  // open: gt, lt
  assign bit_extender_1_out = {{12{1'b0}}, Inst[31:12]};  // Bit_Extender bit_extender_1
  Comparator #(.mode("unsigned"), .width(7)) comparator_4 (
    .a(Inst[6:0]), .b(7'b0110111), .eq(comparator_4_eq));  // open: gt, lt
  Comparator #(.mode("unsigned"), .width(7)) comparator_5 (
    .a(Inst[6:0]), .b(7'b0010111), .eq(comparator_5_eq));  // open: gt, lt
  assign bit_extender_2_out = {{20{Inst[31]}}, Inst[31:20]};  // Bit_Extender bit_extender_2
  or or_1 (or_1_out, comparator_4_eq, comparator_5_eq);
  Comparator #(.mode("unsigned"), .width(7)) comparator_6 (
    .a(Inst[6:0]), .b(7'b0110011), .eq(comparator_6_eq));  // open: gt, lt
  or or_2 (or_2_out, comparator_1_eq, comparator_2_eq, comparator_3_eq);
  Multiplexer #(.width(32)) multiplexer_1 (.in0({32{1'b0}}), .in1({32{1'b0}}), .out(R_type), .sel(comparator_6_eq));
  Multiplexer #(.width(32)) multiplexer_2 (.in0({32{1'b0}}), .in1(bit_extender_2_out), .out(I_type), .sel(or_2_out));
  Multiplexer #(.width(32)) multiplexer_3 (.in0({32{1'b0}}), .in1(bit_extender_1_out), .out(U_type), .sel(or_1_out));
  assign IMM_generate = R_type | I_type | U_type | J_type | B_type | S_type;  // OR_Gate or_3, 32 bits wide
  assign bit_extender_3_out = {{20{Inst[31]}}, {Inst[31], Inst[7], Inst[30:25], Inst[11:8]}};  // Bit_Extender bit_extender_3
  assign bit_extender_4_out = {{12{Inst[31]}}, {Inst[31], Inst[19:12], Inst[20], Inst[30:21]}};  // Bit_Extender bit_extender_4
  Comparator #(.mode("unsigned"), .width(7)) comparator_7 (
    .a(Inst[6:0]), .b(7'b0100011), .eq(comparator_7_eq));  // open: gt, lt
  Comparator #(.mode("unsigned"), .width(7)) comparator_8 (
    .a(Inst[6:0]), .b(7'b1100011), .eq(comparator_8_eq));  // open: gt, lt
  assign bit_extender_5_out = {{20{Inst[31]}}, {Inst[31:25], Inst[11:7]}};  // Bit_Extender bit_extender_5
  Comparator #(.mode("unsigned"), .width(7)) comparator_9 (
    .a(Inst[6:0]), .b(7'b1101111), .eq(comparator_9_eq));  // open: gt, lt
  Shifter #(.width(32)) shifter_1 (.in(bit_extender_3_out), .\dist (5'b00001), .out(shifter_1_out));
  Shifter #(.width(32)) shifter_2 (.in(bit_extender_4_out), .\dist (5'b00001), .out(shifter_2_out));
  Multiplexer #(.width(32)) multiplexer_4 (
    .in0({32{1'b0}}), .in1(bit_extender_5_out), .out(S_type), .sel(comparator_7_eq));
  Multiplexer #(.width(32)) multiplexer_5 (.in0({32{1'b0}}), .in1(shifter_1_out), .out(B_type), .sel(comparator_8_eq));
  Multiplexer #(.width(32)) multiplexer_6 (.in0({32{1'b0}}), .in1(shifter_2_out), .out(J_type), .sel(comparator_9_eq));

  // Other names for the same wires on the sheet: B_type_num[11:0] = {Inst[31], Inst[7], Inst[30:25], Inst[11:8]};
  //   S_type_num[11:0] = {Inst[31:25], Inst[11:7]}; IMM_Gen[31:0] = IMM_generate; Opcode[6:0] = Inst[6:0];
  //   I_type_12_num[11:0] = Inst[31:20]; J_type_num[19:0] = {Inst[31], Inst[19:12], Inst[20], Inst[30:21]};
  //   U_type_20_num_unsigned[19:0] = Inst[31:12]

  // Notes on the sheet:
  //   input: inst
  //   hardcode: 
  //   I type: 0x13
  //   I type: 0x03
  //   I type : 0x67
  //   s type:0x23
  //   J type:0x6f
  //   B type: 0x63
  //   R type:0x33
  //   Utype: 0x37/0x17
endmodule

module ALU (
  input  [3:0] Inst_id,
  input  [31:0] Current_pc,
  input  [31:0] Data_A,
  input  [31:0] Data_B,
  input  [31:0] IMM,
  output [31:0] ALU_OUT,
  output [31:0] NEW_PC,
  output Jump
);

  wire and_2_out, comparator_1_lt, comparator_2_lt, comparator_3_lt, comparator_4_eq, comparator_5_eq,
       comparator_6_eq, comparator_7_eq;
  wire [4:0] multiplexer_1_out;
  wire [31:0] ADD_type0, ADDI_type6, ANDI_type5, AUIPC_type10, JAL_type14, JALR_type9, LH_type8, LUI_type11,
       LW_type7, NEW_PC_beq, NEW_PC_jal, NEW_PC_jalr, SH_type13, shifter_1_out, SLITU_type4, SLT_type2,
       SRA_type1, SRLI_type3, SW_type12;

  Multiplexer #(.width(5)) multiplexer_1 (
    .in0({5{1'b0}}), .in1(IMM[4:0]), .out(multiplexer_1_out), .sel(comparator_1_lt));
  Comparator #(.width(32)) comparator_1 (.a(IMM), .b(32'h20), .lt(comparator_1_lt));  // open: gt, eq
  Shifter #(.width(32)) shifter_1 (.in(IMM), .\dist (5'b01100), .out(shifter_1_out));
  Comparator #(.width(32)) comparator_2 (.a(Data_A), .b(Data_B), .lt(comparator_2_lt));  // open: gt, eq
  assign SLT_type2 = {{31{1'b0}}, comparator_2_lt};  // Bit_Extender bit_extender_1
  Shifter #(.shift("lr"), .width(32)) shifter_2 (.in(Data_A), .\dist (multiplexer_1_out), .out(SRLI_type3));
  Comparator #(.mode("unsigned"), .width(32)) comparator_3 (.a(Data_A), .b(IMM), .lt(comparator_3_lt));  // open: gt, eq
  assign SLITU_type4 = {{31{1'b0}}, comparator_3_lt};  // Bit_Extender bit_extender_2
  assign ANDI_type5 = Data_A & IMM;  // AND_Gate and_1, 32 bits wide
  Adder #(.width(32)) adder_1 (.a(Data_A), .b(IMM), .out(ADDI_type6));  // open: cin, cout
  Adder #(.width(32)) adder_2 (.a(Data_A), .b(IMM), .out(LW_type7));  // open: cin, cout
  Adder #(.width(32)) adder_3 (.a(Data_A), .b(IMM), .out(LH_type8));  // open: cin, cout
  Adder #(.width(32)) adder_4 (.a(Current_pc), .b(32'h4), .out(JALR_type9));  // open: cin, cout
  Adder #(.width(32)) adder_5 (.a(Data_A), .b(IMM), .out(NEW_PC_jalr));  // open: cin, cout
  Adder #(.width(32)) adder_6 (.a(Current_pc), .b(shifter_1_out), .out(AUIPC_type10));  // open: cin, cout
  Adder #(.width(32)) adder_7 (.a(Data_A), .b(Data_B), .out(ADD_type0));  // open: cin, cout
  Shifter #(.shift("ar"), .width(32)) shifter_3 (.in(Data_A), .\dist (Data_B[4:0]), .out(SRA_type1));
  Comparator #(.width(32)) comparator_4 (.a(Data_A), .b(Data_B), .eq(comparator_4_eq));  // open: gt, lt
  Comparator #(.width(4)) comparator_5 (.a(Inst_id), .b(4'b1111), .eq(comparator_5_eq));  // open: gt, lt
  and and_2 (and_2_out, comparator_4_eq, comparator_5_eq);
  Comparator #(.width(4)) comparator_6 (.a(Inst_id), .b(4'b1110), .eq(comparator_6_eq));  // open: gt, lt
  Comparator #(.width(4)) comparator_7 (.a(Inst_id), .b(4'b1001), .eq(comparator_7_eq));  // open: gt, lt
  or or_1 (Jump, and_2_out, comparator_6_eq, comparator_7_eq);
  Adder #(.width(32)) adder_8 (.a(Data_A), .b(IMM), .out(SW_type12));  // open: cin, cout
  Adder #(.width(32)) adder_9 (.a(Data_A), .b(IMM), .out(SH_type13));  // open: cin, cout
  Shifter #(.width(32)) shifter_4 (.in(IMM), .\dist (5'b01100), .out(LUI_type11));
  Adder #(.width(32)) adder_10 (.a(Current_pc), .b(32'h4), .out(JAL_type14));  // open: cin, cout
  Adder #(.width(32)) adder_11 (.a(Current_pc), .b(IMM), .out(NEW_PC_jal));  // open: cin, cout
  Adder #(.width(32)) adder_12 (.a(Current_pc), .b(IMM), .out(NEW_PC_beq));  // open: cin, cout
  Multiplexer #(.select(4), .width(32)) multiplexer_2 (
    .in0(ADD_type0), .in1(SRA_type1), .in2(SLT_type2), .in3(SRLI_type3), .in4(SLITU_type4), .in5(ANDI_type5),
    .in6(ADDI_type6), .in7(LW_type7), .in8(LH_type8), .in9(JALR_type9), .in10(AUIPC_type10),
    .in11(LUI_type11), .in12(SW_type12), .in13(SH_type13), .in14(JAL_type14), .in15(NEW_PC_beq),
    .out(ALU_OUT), .sel(Inst_id));
  Multiplexer #(.select(4), .width(32)) multiplexer_3 (
    .in0(ADD_type0), .in1(SRA_type1), .in2(SLT_type2), .in3(SRLI_type3), .in4(SLITU_type4), .in5(ANDI_type5),
    .in6(ADDI_type6), .in7(LW_type7), .in8(LH_type8), .in9(NEW_PC_jalr), .in10(AUIPC_type10),
    .in11(LUI_type11), .in12(SW_type12), .in13(SH_type13), .in14(NEW_PC_jal), .in15(NEW_PC_beq),
    .out(NEW_PC), .sel(Inst_id));
endmodule

module DMEM (
  input  rst,
  input  Write_half,
  input  Read_half,
  input  [31:0] Addr,
  input  [31:0] data_D,
  input  MemRW,
  input  clk,
  output [31:0] DATA_output
);

  wire and_1_out, and_2_out, and_3_out, and_4_out, comparator_1_lt, comparator_2_lt, comparator_3_lt,
       comparator_4_lt, comparator_5_eq, comparator_6_eq, comparator_7_eq, comparator_8_eq, comparator_9_eq,
       comparator_10_eq, comparator_11_eq, comparator_12_eq, comparator_13_eq, comparator_14_eq,
       comparator_15_eq, comparator_16_eq, comparator_17_eq, comparator_18_eq, comparator_19_eq,
       comparator_20_eq, comparator_21_eq, comparator_22_eq, comparator_23_eq, comparator_24_eq, MEM0, MEM00,
       MEM01, MEM1, MEM02, MEM2, MEM03, MEM3, MEM10, MEM11, MEM12, MEM13, MEM20, MEM21, MEM22, MEM23, MEM30,
       MEM31, MEM32, MEM33, not_1_out, not_2_out, or_9_out, or_10_out, or_11_out, or_12_out, or_13_out,
       or_14_out, or_15_out, or_16_out, or_17_out, or_18_out, or_19_out, or_20_out;
  wire [1:0] check_0, check_1, check_2, check_3, mod1, mod2, mod3, multiplexer_12_out, multiplexer_14_out,
       multiplexer_16_out, multiplexer_18_out;
  wire [2:0] bit_extender_1_out, bit_extender_2_out, bit_extender_5_out, bit_extender_7_out,
       subtractor_1_out, subtractor_2_out, subtractor_3_out, subtractor_4_out;
  wire [7:0] Byte_output_0, Byte_output_1, Byte_output_2, Byte_output_3, multiplexer_3_out,
       multiplexer_4_out, output_0, output_1, output_2, output_3, RAM0, RAM00, RAM01, RAM1, RAM02, RAM2,
       RAM03, RAM3, RAM10, RAM11, RAM12, RAM13, RAM20, RAM21, RAM22, RAM23, RAM30, RAM31, RAM32, RAM33;
  wire [13:0] Addr_new_0, Addr_new_1, Addr_new_2, Addr_new_3, bit_extender_3_out, bit_extender_4_out,
       bit_extender_6_out, bit_extender_8_out;
  wire [31:0] adder_1_out, adder_2_out, adder_3_out, adder_5_out, adder_6_out, adder_7_out, adder_11_out,
       adder_12_out, adder_13_out, bit_extender_9_out;
  wire [31:2] adder_14_out, adder_15_out, adder_16_out;

  assign bit_extender_1_out = {{1{1'b0}}, check_0};  // Bit_Extender bit_extender_1
  assign bit_extender_2_out = {{1{1'b0}}, check_1};  // Bit_Extender bit_extender_2
  Demultiplexer #(.select(2), .width(8)) demultiplexer_1 (
    .out0(RAM00), .out1(RAM10), .out2(RAM20), .out3(RAM30), .in(data_D[7:0]), .sel(Addr[1:0]));
  Adder #(.width(32)) adder_1 (.a(Addr), .b(32'h1), .out(adder_1_out));  // open: cin, cout
  Adder #(.width(32)) adder_2 (.a(Addr), .b(32'h2), .out(adder_2_out));  // open: cin, cout
  Adder #(.width(32)) adder_3 (.a(Addr), .b(32'h3), .out(adder_3_out));  // open: cin, cout
  Subtractor #(.width(3)) subtractor_1 (.a(3'b000), .b(bit_extender_1_out), .out(subtractor_1_out));  // open: bin, bout
  Subtractor #(.width(3)) subtractor_2 (.a(3'b001), .b(bit_extender_2_out), .out(subtractor_2_out));  // open: bin, bout
  Demultiplexer #(.select(2), .width(8)) demultiplexer_2 (
    .out0(RAM01), .out1(RAM11), .out2(RAM21), .out3(RAM31), .in(data_D[15:8]), .sel(adder_1_out[1:0]));
  Demultiplexer #(.select(2), .width(8)) demultiplexer_3 (
    .out0(RAM02), .out1(RAM12), .out2(RAM22), .out3(RAM32), .in(data_D[23:16]), .sel(adder_2_out[1:0]));
  Demultiplexer #(.select(2), .width(8)) demultiplexer_4 (
    .out0(RAM03), .out1(RAM13), .out2(RAM23), .out3(RAM33), .in(data_D[31:24]), .sel(adder_3_out[1:0]));
  assign bit_extender_3_out = {{13{1'b0}}, comparator_1_lt};  // Bit_Extender bit_extender_3
  assign bit_extender_4_out = {{13{1'b0}}, comparator_2_lt};  // Bit_Extender bit_extender_4
  Subtractor #(.width(3)) subtractor_3 (.a(3'b010), .b(bit_extender_5_out), .out(subtractor_3_out));  // open: bin, bout
  assign bit_extender_5_out = {{1{1'b0}}, check_2};  // Bit_Extender bit_extender_5
  Comparator #(.width(3)) comparator_1 (.a(subtractor_1_out), .b(3'b000), .lt(comparator_1_lt));  // open: gt, eq
  Comparator #(.width(3)) comparator_2 (.a(subtractor_2_out), .b(3'b000), .lt(comparator_2_lt));  // open: gt, eq
  Adder #(.width(14)) adder_4 (.a(Addr[15:2]), .b(bit_extender_4_out), .out(Addr_new_1));  // open: cin, cout
  assign bit_extender_6_out = {{13{1'b0}}, comparator_3_lt};  // Bit_Extender bit_extender_6
  Comparator #(.width(3)) comparator_3 (.a(subtractor_3_out), .b(3'b000), .lt(comparator_3_lt));  // open: gt, eq
  Adder #(.width(32)) adder_5 (.a(Addr), .b(32'h1), .out(adder_5_out));  // open: cin, cout
  not not_1 (not_1_out, Write_half);
  Adder #(.width(32)) adder_6 (.a(Addr), .b(32'h2), .out(adder_6_out));  // open: cin, cout
  not not_2 (not_2_out, Write_half);
  Adder #(.width(32)) adder_7 (.a(Addr), .b(32'h3), .out(adder_7_out));  // open: cin, cout
  Adder #(.width(14)) adder_8 (.a(Addr[15:2]), .b(bit_extender_3_out), .out(Addr_new_0));  // open: cin, cout
  RAM #(.addrWidth(14), .asyncread("true"), .clearpin("true"), .trigger("falling")) ram_1 (
    .addr(Addr_new_0), .we(MEM0), .oe(1'b1), .clk(clk), .din(RAM0), .dout(output_0), .clr(rst));
  RAM #(.addrWidth(14), .asyncread("true"), .clearpin("true"), .trigger("falling")) ram_2 (
    .addr(Addr_new_2), .we(MEM2), .oe(1'b1), .clk(clk), .din(RAM2), .dout(output_2), .clr(rst));
  Adder #(.width(14)) adder_9 (.a(Addr[15:2]), .b(bit_extender_6_out), .out(Addr_new_2));  // open: cin, cout
  Demultiplexer #(.select(2)) demultiplexer_5 (
    .out0(MEM00), .out1(MEM10), .out2(MEM20), .out3(MEM30), .in(and_1_out), .sel(Addr[1:0]));
  and and_1 (and_1_out, 1'b1, MemRW);
  Demultiplexer #(.select(2)) demultiplexer_6 (
    .out0(MEM01), .out1(MEM11), .out2(MEM21), .out3(MEM31), .in(and_2_out), .sel(adder_5_out[1:0]));
  and and_2 (and_2_out, 1'b1, MemRW);
  Demultiplexer #(.select(2)) demultiplexer_7 (
    .out0(MEM02), .out1(MEM12), .out2(MEM22), .out3(MEM32), .in(and_3_out), .sel(adder_6_out[1:0]));
  and and_3 (and_3_out, 1'b1, not_1_out, MemRW);
  and and_4 (and_4_out, 1'b1, not_2_out, MemRW);
  assign bit_extender_7_out = {{1{1'b0}}, check_2};  // Bit_Extender bit_extender_7
  Demultiplexer #(.select(2)) demultiplexer_8 (
    .out0(MEM03), .out1(MEM13), .out2(MEM23), .out3(MEM33), .in(and_4_out), .sel(adder_7_out[1:0]));
  Subtractor #(.width(3)) subtractor_4 (.a(3'b011), .b(bit_extender_7_out), .out(subtractor_4_out));  // open: bin, bout
  assign bit_extender_8_out = {{13{1'b0}}, comparator_4_lt};  // Bit_Extender bit_extender_8
  Comparator #(.width(3)) comparator_4 (.a(subtractor_4_out), .b(3'b000), .lt(comparator_4_lt));  // open: gt, eq
  Adder #(.width(14)) adder_10 (.a(Addr[15:2]), .b(bit_extender_8_out), .out(Addr_new_3));  // open: cin, cout
  RAM #(.addrWidth(14), .asyncread("true"), .clearpin("true"), .trigger("falling")) ram_3 (
    .addr(Addr_new_1), .we(MEM1), .oe(1'b1), .clk(clk), .din(RAM1), .dout(output_1), .clr(rst));
  RAM #(.addrWidth(14), .asyncread("true"), .clearpin("true"), .trigger("falling")) ram_4 (
    .addr(Addr_new_3), .we(MEM3), .oe(1'b1), .clk(clk), .din(RAM3), .dout(output_3), .clr(rst));
  assign RAM0 = RAM00 | RAM01 | RAM02 | RAM03;  // OR_Gate or_1, 8 bits wide
  assign RAM1 = RAM10 | RAM11 | RAM12 | RAM13;  // OR_Gate or_2, 8 bits wide
  assign RAM2 = RAM20 | RAM21 | RAM22 | RAM23;  // OR_Gate or_3, 8 bits wide
  assign RAM3 = RAM30 | RAM31 | RAM32 | RAM33;  // OR_Gate or_4, 8 bits wide
  or or_5 (MEM0, MEM00, MEM01, MEM02, MEM03);
  or or_6 (MEM1, MEM10, MEM11, MEM12, MEM13);
  or or_7 (MEM2, MEM20, MEM21, MEM22, MEM23);
  or or_8 (MEM3, MEM30, MEM31, MEM32, MEM33);
  Adder #(.width(32)) adder_11 (.a(Addr), .b(32'h1), .out(adder_11_out));  // open: cin, cout
  Adder #(.width(32)) adder_12 (.a(Addr), .b(32'h2), .out(adder_12_out));  // open: cin, cout
  Adder #(.width(32)) adder_13 (.a(Addr), .b(32'h3), .out(adder_13_out));  // open: cin, cout
  Multiplexer #(.select(2), .width(8)) multiplexer_1 (
    .in0(output_0), .in1(output_1), .in2(output_2), .in3(output_3), .out(Byte_output_0), .sel(Addr[1:0]));
  Multiplexer #(.select(2), .width(8)) multiplexer_2 (
    .in0(output_0), .in1(output_1), .in2(output_2), .in3(output_3), .out(Byte_output_1),
    .sel(adder_11_out[1:0]));
  Multiplexer #(.select(2), .width(8)) multiplexer_3 (
    .in0(output_0), .in1(output_1), .in2(output_2), .in3(output_3), .out(multiplexer_3_out),
    .sel(adder_12_out[1:0]));
  Multiplexer #(.select(2), .width(8)) multiplexer_4 (
    .in0(output_0), .in1(output_1), .in2(output_2), .in3(output_3), .out(multiplexer_4_out),
    .sel(adder_13_out[1:0]));
  Multiplexer #(.width(8)) multiplexer_5 (
    .in0(multiplexer_3_out), .in1({8{1'b0}}), .out(Byte_output_2), .sel(Read_half));
  Multiplexer #(.width(8)) multiplexer_6 (
    .in0(multiplexer_4_out), .in1({8{1'b0}}), .out(Byte_output_3), .sel(Read_half));
  assign bit_extender_9_out = {{16{Byte_output_1[7]}}, {Byte_output_1, Byte_output_0}};  // Bit_Extender bit_extender_9
  Multiplexer #(.select(2), .width(2)) multiplexer_7 (
    .in0(2'b00), .in1(2'b01), .in2(2'b10), .in3(2'b11), .out(check_0), .sel(multiplexer_12_out));
  Multiplexer #(.select(2), .width(2)) multiplexer_8 (
    .in0(2'b00), .in1(2'b01), .in2(2'b10), .in3(2'b11), .out(check_1), .sel(multiplexer_14_out));
  Multiplexer #(.select(2), .width(2)) multiplexer_9 (
    .in0(2'b00), .in1(2'b01), .in2(2'b10), .in3(2'b11), .out(check_2), .sel(multiplexer_16_out));
  Multiplexer #(.width(32)) multiplexer_10 (
    .in0({Byte_output_3, Byte_output_2, Byte_output_1, Byte_output_0}), .in1(bit_extender_9_out),
    .out(DATA_output), .sel(Read_half));
  Multiplexer #(.select(2), .width(2)) multiplexer_11 (
    .in0(2'b00), .in1(2'b01), .in2(2'b10), .in3(2'b11), .out(check_3), .sel(multiplexer_18_out));
  Multiplexer multiplexer_12 (.in0(1'b0), .in1(1'b1), .out(multiplexer_12_out[0]), .sel(or_9_out));
  Multiplexer multiplexer_13 (.in0(or_10_out), .in1(1'b0), .out(multiplexer_12_out[1]), .sel(or_11_out));
  Multiplexer multiplexer_14 (.in0(1'b0), .in1(1'b1), .out(multiplexer_14_out[0]), .sel(or_12_out));
  or or_9 (or_9_out, comparator_6_eq, comparator_7_eq);
  or or_10 (or_10_out, comparator_5_eq, comparator_7_eq, comparator_8_eq, comparator_9_eq);
  or or_11 (or_11_out, comparator_8_eq, comparator_9_eq);
  or or_12 (or_12_out, comparator_11_eq, comparator_12_eq);
  or or_13 (or_13_out, comparator_10_eq, comparator_12_eq, comparator_13_eq, comparator_14_eq);
  Multiplexer multiplexer_15 (.in0(or_13_out), .in1(1'b0), .out(multiplexer_14_out[1]), .sel(or_14_out));
  Multiplexer multiplexer_16 (.in0(1'b0), .in1(1'b1), .out(multiplexer_16_out[0]), .sel(or_15_out));
  Multiplexer multiplexer_17 (.in0(or_16_out), .in1(1'b0), .out(multiplexer_16_out[1]), .sel(or_17_out));
  Multiplexer multiplexer_18 (.in0(1'b0), .in1(1'b1), .out(multiplexer_18_out[0]), .sel(or_18_out));
  Multiplexer multiplexer_19 (.in0(or_19_out), .in1(1'b0), .out(multiplexer_18_out[1]), .sel(or_20_out));
  or or_14 (or_14_out, comparator_13_eq, comparator_14_eq);
  or or_15 (or_15_out, comparator_16_eq, comparator_17_eq);
  or or_16 (or_16_out, comparator_15_eq, comparator_17_eq, comparator_18_eq, comparator_19_eq);
  or or_17 (or_17_out, comparator_18_eq, comparator_19_eq);
  or or_18 (or_18_out, comparator_21_eq, comparator_22_eq);
  or or_19 (or_19_out, comparator_20_eq, comparator_22_eq, comparator_23_eq, comparator_24_eq);
  or or_20 (or_20_out, comparator_23_eq, comparator_24_eq);
  Comparator #(.mode("unsigned"), .width(2)) comparator_5 (.a(mod2), .b(2'b00), .eq(comparator_5_eq));  // open: gt, lt
  Comparator #(.mode("unsigned"), .width(2)) comparator_6 (.a(mod1), .b(2'b00), .eq(comparator_6_eq));  // open: gt, lt
  Comparator #(.mode("unsigned"), .width(2)) comparator_7 (.a(mod3), .b(2'b00), .eq(comparator_7_eq));  // open: gt, lt
  Comparator #(.mode("unsigned"), .width(2)) comparator_8 (
    .a(Addr[1:0]), .b(2'b00), .eq(comparator_8_eq));  // open: gt, lt
  Adder #(.width(32)) adder_14 (.a(Addr), .b(32'h3), .out({adder_14_out, mod3}));  // open: cin, cout
  Adder #(.width(32)) adder_15 (.a(Addr), .b(32'h2), .out({adder_15_out, mod2}));  // open: cin, cout
  Adder #(.width(32)) adder_16 (.a(Addr), .b(32'h1), .out({adder_16_out, mod1}));  // open: cin, cout
  Comparator #(.mode("unsigned"), .width(2)) comparator_9 (.a(mod1), .b(2'b00), .eq(comparator_9_eq));  // open: gt, lt
  Comparator #(.mode("unsigned"), .width(2)) comparator_10 (
    .a(mod2), .b(2'b01), .eq(comparator_10_eq));  // open: gt, lt
  Comparator #(.mode("unsigned"), .width(2)) comparator_11 (
    .a(mod1), .b(2'b01), .eq(comparator_11_eq));  // open: gt, lt
  Comparator #(.mode("unsigned"), .width(2)) comparator_12 (
    .a(mod3), .b(2'b01), .eq(comparator_12_eq));  // open: gt, lt
  Comparator #(.mode("unsigned"), .width(2)) comparator_13 (
    .a(Addr[1:0]), .b(2'b01), .eq(comparator_13_eq));  // open: gt, lt
  Comparator #(.mode("unsigned"), .width(2)) comparator_14 (
    .a(mod1), .b(2'b01), .eq(comparator_14_eq));  // open: gt, lt
  Comparator #(.mode("unsigned"), .width(2)) comparator_15 (
    .a(mod2), .b(2'b10), .eq(comparator_15_eq));  // open: gt, lt
  Comparator #(.mode("unsigned"), .width(2)) comparator_16 (
    .a(mod1), .b(2'b10), .eq(comparator_16_eq));  // open: gt, lt
  Comparator #(.mode("unsigned"), .width(2)) comparator_17 (
    .a(mod3), .b(2'b10), .eq(comparator_17_eq));  // open: gt, lt
  Comparator #(.mode("unsigned"), .width(2)) comparator_18 (
    .a(Addr[1:0]), .b(2'b10), .eq(comparator_18_eq));  // open: gt, lt
  Comparator #(.mode("unsigned"), .width(2)) comparator_19 (
    .a(mod1), .b(2'b10), .eq(comparator_19_eq));  // open: gt, lt
  Comparator #(.mode("unsigned"), .width(2)) comparator_20 (
    .a(mod2), .b(2'b11), .eq(comparator_20_eq));  // open: gt, lt
  Comparator #(.mode("unsigned"), .width(2)) comparator_21 (
    .a(mod1), .b(2'b11), .eq(comparator_21_eq));  // open: gt, lt
  Comparator #(.mode("unsigned"), .width(2)) comparator_22 (
    .a(mod3), .b(2'b11), .eq(comparator_22_eq));  // open: gt, lt
  Comparator #(.mode("unsigned"), .width(2)) comparator_23 (
    .a(Addr[1:0]), .b(2'b11), .eq(comparator_23_eq));  // open: gt, lt
  Comparator #(.mode("unsigned"), .width(2)) comparator_24 (
    .a(mod1), .b(2'b11), .eq(comparator_24_eq));  // open: gt, lt

  // Other names for the same wires on the sheet: mod0[1:0] = Addr[1:0]; Addr_temp[13:0] = Addr[15:2];
  //   byte1[7:0] = data_D[7:0]; byte2[7:0] = data_D[15:8]; byte3[7:0] = data_D[23:16]; byte4[7:0] = data_D[31:24]
endmodule

module Control_logic (
  input  [31:0] Inst,
  input  Is_equal,
  output PCsel,
  output WB_sel,
  output RegWEn,
  output [3:0] inst_id,
  output MemRW,
  output Write_half,
  output Read_half
);

  wire ADD_type, ADDI_type, and_3_out, ANDI_type, AUIPC_type, BEQ_type, comparator_1_eq, comparator_2_eq,
       comparator_7_eq, comparator_8_eq, comparator_9_eq, comparator_10_eq, comparator_11_eq,
       comparator_12_eq, comparator_13_eq, comparator_14_eq, comparator_15_eq, comparator_16_eq,
       comparator_17_eq, comparator_18_eq, comparator_19_eq, comparator_20_eq, comparator_21_eq,
       comparator_22_eq, comparator_23_eq, comparator_24_eq, comparator_25_eq, comparator_26_eq,
       comparator_27_eq, comparator_28_eq, JAL_type, JALR_type, LH_type, LUI_type, LW_type,
       multiplexer_17_out, multiplexer_18_out, multiplexer_19_out, multiplexer_20_out, multiplexer_21_out,
       multiplexer_22_out, multiplexer_23_out, multiplexer_24_out, multiplexer_25_out, multiplexer_26_out,
       multiplexer_27_out, multiplexer_28_out, multiplexer_29_out, multiplexer_30_out, multiplexer_31_out,
       multiplexer_32_out, multiplexer_33_out, multiplexer_34_out, multiplexer_35_out, multiplexer_36_out,
       multiplexer_37_out, multiplexer_38_out, multiplexer_39_out, multiplexer_40_out, multiplexer_41_out,
       multiplexer_42_out, multiplexer_43_out, multiplexer_44_out, multiplexer_45_out, multiplexer_46_out,
       multiplexer_47_out, multiplexer_48_out, multiplexer_49_out, multiplexer_50_out, multiplexer_51_out,
       multiplexer_52_out, multiplexer_53_out, multiplexer_54_out, multiplexer_55_out, multiplexer_56_out,
       multiplexer_57_out, multiplexer_58_out, multiplexer_59_out, multiplexer_60_out, multiplexer_61_out,
       multiplexer_62_out, multiplexer_63_out, multiplexer_64_out, multiplexer_65_out, multiplexer_66_out,
       multiplexer_67_out, multiplexer_68_out, multiplexer_69_out, multiplexer_70_out, multiplexer_71_out,
       multiplexer_72_out, multiplexer_73_out, multiplexer_74_out, multiplexer_75_out, multiplexer_76_out,
       multiplexer_77_out, multiplexer_78_out, multiplexer_79_out, multiplexer_80_out, multiplexer_81_out,
       multiplexer_82_out, multiplexer_83_out, multiplexer_84_out, multiplexer_85_out, multiplexer_86_out,
       multiplexer_87_out, multiplexer_88_out, multiplexer_89_out, multiplexer_90_out, multiplexer_91_out,
       multiplexer_92_out, multiplexer_93_out, multiplexer_94_out, multiplexer_95_out, multiplexer_96_out,
       multiplexer_97_out, multiplexer_98_out, multiplexer_99_out, multiplexer_100_out, multiplexer_101_out,
       multiplexer_102_out, multiplexer_103_out, multiplexer_104_out, multiplexer_105_out,
       multiplexer_106_out, multiplexer_107_out, multiplexer_108_out, multiplexer_109_out,
       multiplexer_110_out, multiplexer_111_out, multiplexer_112_out, SH_type, SLT_type, SLTIU_type,
       SRA_type, SRLI_type, SW_type;
  wire [3:0] multiplexer_1_out, multiplexer_2_out, multiplexer_3_out, multiplexer_4_out, multiplexer_5_out,
       multiplexer_6_out, multiplexer_7_out, multiplexer_8_out, multiplexer_9_out, multiplexer_10_out,
       multiplexer_11_out, multiplexer_12_out, multiplexer_13_out, multiplexer_14_out, multiplexer_15_out,
       multiplexer_16_out;

  Comparator #(.mode("unsigned"), .width(7)) comparator_1 (
    .a(Inst[6:0]), .b(7'b0000011), .eq(comparator_1_eq));  // open: gt, lt
  Comparator #(.mode("unsigned"), .width(3)) comparator_2 (
    .a(Inst[14:12]), .b(3'b001), .eq(comparator_2_eq));  // open: gt, lt
  Multiplexer #(.width(4)) multiplexer_1 (.in0(4'b0000), .in1(4'b0000), .out(multiplexer_1_out), .sel(ADD_type));
  Multiplexer #(.width(4)) multiplexer_2 (.in0(4'b0000), .in1(4'b0001), .out(multiplexer_2_out), .sel(SRA_type));
  Multiplexer #(.width(4)) multiplexer_3 (.in0(4'b0000), .in1(4'b0010), .out(multiplexer_3_out), .sel(SLT_type));
  Multiplexer #(.width(4)) multiplexer_4 (.in0(4'b0000), .in1(4'b0011), .out(multiplexer_4_out), .sel(SRLI_type));
  Multiplexer #(.width(4)) multiplexer_5 (.in0(4'b0000), .in1(4'b0100), .out(multiplexer_5_out), .sel(SLTIU_type));
  Multiplexer #(.width(4)) multiplexer_6 (.in0(4'b0000), .in1(4'b0101), .out(multiplexer_6_out), .sel(ANDI_type));
  Multiplexer #(.width(4)) multiplexer_7 (.in0(4'b0000), .in1(4'b0110), .out(multiplexer_7_out), .sel(ADDI_type));
  Multiplexer #(.width(4)) multiplexer_8 (.in0(4'b0000), .in1(4'b0111), .out(multiplexer_8_out), .sel(LW_type));
  Multiplexer #(.width(4)) multiplexer_9 (.in0(4'b0000), .in1(4'b1000), .out(multiplexer_9_out), .sel(LH_type));
  Multiplexer #(.width(4)) multiplexer_10 (.in0(4'b0000), .in1(4'b1001), .out(multiplexer_10_out), .sel(JALR_type));
  Multiplexer #(.width(4)) multiplexer_11 (.in0(4'b0000), .in1(4'b1010), .out(multiplexer_11_out), .sel(AUIPC_type));
  Multiplexer #(.width(4)) multiplexer_12 (.in0(4'b0000), .in1(4'b1011), .out(multiplexer_12_out), .sel(LUI_type));
  Multiplexer #(.width(4)) multiplexer_13 (.in0(4'b0000), .in1(4'b1100), .out(multiplexer_13_out), .sel(SW_type));
  Multiplexer #(.width(4)) multiplexer_14 (.in0(4'b0000), .in1(4'b1101), .out(multiplexer_14_out), .sel(SH_type));
  Multiplexer #(.width(4)) multiplexer_15 (.in0(4'b0000), .in1(4'b1110), .out(multiplexer_15_out), .sel(JAL_type));
  Multiplexer #(.width(4)) multiplexer_16 (.in0(4'b0000), .in1(4'b1111), .out(multiplexer_16_out), .sel(BEQ_type));
  Comparator #(.mode("unsigned"), .width(7)) comparator_3 (
    .a(Inst[6:0]), .b(7'b0110111), .eq(LUI_type));  // open: gt, lt
  Comparator #(.mode("unsigned"), .width(7)) comparator_4 (
    .a(Inst[6:0]), .b(7'b0010111), .eq(AUIPC_type));  // open: gt, lt
  Comparator #(.mode("unsigned"), .width(7)) comparator_5 (
    .a(Inst[6:0]), .b(7'b1101111), .eq(JAL_type));  // open: gt, lt
  Comparator #(.mode("unsigned"), .width(7)) comparator_6 (
    .a(Inst[6:0]), .b(7'b1100111), .eq(JALR_type));  // open: gt, lt
  Comparator #(.mode("unsigned"), .width(7)) comparator_7 (
    .a(Inst[6:0]), .b(7'b1100011), .eq(comparator_7_eq));  // open: gt, lt
  Comparator #(.mode("unsigned"), .width(3)) comparator_8 (
    .a(Inst[14:12]), .b(3'b000), .eq(comparator_8_eq));  // open: gt, lt
  and and_1 (BEQ_type, comparator_7_eq, comparator_8_eq);
  and and_2 (LH_type, comparator_1_eq, comparator_2_eq);
  Multiplexer multiplexer_17 (.in0(1'b0), .in1(1'b0), .out(multiplexer_17_out), .sel(ADD_type));
  Multiplexer multiplexer_18 (.in0(1'b0), .in1(1'b0), .out(multiplexer_18_out), .sel(SRA_type));
  Multiplexer multiplexer_19 (.in0(1'b0), .in1(1'b0), .out(multiplexer_19_out), .sel(SLT_type));
  Multiplexer multiplexer_20 (.in0(1'b0), .in1(1'b0), .out(multiplexer_20_out), .sel(SRLI_type));
  Multiplexer multiplexer_21 (.in0(1'b0), .in1(1'b0), .out(multiplexer_21_out), .sel(SLTIU_type));
  Multiplexer multiplexer_22 (.in0(1'b0), .in1(1'b0), .out(multiplexer_22_out), .sel(ANDI_type));
  Multiplexer multiplexer_23 (.in0(1'b0), .in1(1'b0), .out(multiplexer_23_out), .sel(ADDI_type));
  Multiplexer multiplexer_24 (.in0(1'b0), .in1(1'b0), .out(multiplexer_24_out), .sel(LW_type));
  Multiplexer multiplexer_25 (.in0(1'b0), .in1(1'b0), .out(multiplexer_25_out), .sel(LH_type));
  Multiplexer multiplexer_26 (.in0(1'b0), .in1(1'b1), .out(multiplexer_26_out), .sel(JALR_type));
  Multiplexer multiplexer_27 (.in0(1'b0), .in1(1'b0), .out(multiplexer_27_out), .sel(AUIPC_type));
  Multiplexer multiplexer_28 (.in0(1'b0), .in1(1'b0), .out(multiplexer_28_out), .sel(LUI_type));
  Multiplexer multiplexer_29 (.in0(1'b0), .in1(1'b0), .out(multiplexer_29_out), .sel(SW_type));
  Multiplexer multiplexer_30 (.in0(1'b0), .in1(1'b0), .out(multiplexer_30_out), .sel(SH_type));
  Multiplexer multiplexer_31 (.in0(1'b0), .in1(1'b1), .out(multiplexer_31_out), .sel(JAL_type));
  Multiplexer multiplexer_32 (.in0(1'b0), .in1(1'b1), .out(multiplexer_32_out), .sel(BEQ_type));
  Comparator #(.mode("unsigned"), .width(7)) comparator_9 (
    .a(Inst[6:0]), .b(7'b0000011), .eq(comparator_9_eq));  // open: gt, lt
  Comparator #(.mode("unsigned"), .width(3)) comparator_10 (
    .a(Inst[14:12]), .b(3'b010), .eq(comparator_10_eq));  // open: gt, lt
  Comparator #(.mode("unsigned"), .width(7)) comparator_11 (
    .a(Inst[6:0]), .b(7'b0100011), .eq(comparator_11_eq));  // open: gt, lt
  Comparator #(.mode("unsigned"), .width(3)) comparator_12 (
    .a(Inst[14:12]), .b(3'b010), .eq(comparator_12_eq));  // open: gt, lt
  Comparator #(.mode("unsigned"), .width(7)) comparator_13 (
    .a(Inst[6:0]), .b(7'b0100011), .eq(comparator_13_eq));  // open: gt, lt
  Comparator #(.mode("unsigned"), .width(3)) comparator_14 (
    .a(Inst[14:12]), .b(3'b001), .eq(comparator_14_eq));  // open: gt, lt
  Comparator #(.mode("unsigned"), .width(7)) comparator_15 (
    .a(Inst[6:0]), .b(7'b0010011), .eq(comparator_15_eq));  // open: gt, lt
  Comparator #(.mode("unsigned"), .width(3)) comparator_16 (
    .a(Inst[14:12]), .b(3'b000), .eq(comparator_16_eq));  // open: gt, lt
  Comparator #(.mode("unsigned"), .width(7)) comparator_17 (
    .a(Inst[6:0]), .b(7'b0010011), .eq(comparator_17_eq));  // open: gt, lt
  Comparator #(.mode("unsigned"), .width(3)) comparator_18 (
    .a(Inst[14:12]), .b(3'b011), .eq(comparator_18_eq));  // open: gt, lt
  and and_3 (and_3_out, multiplexer_32_out, Is_equal);
  and and_4 (LW_type, comparator_9_eq, comparator_10_eq);
  and and_5 (SW_type, comparator_11_eq, comparator_12_eq);
  and and_6 (SH_type, comparator_13_eq, comparator_14_eq);
  and and_7 (ADDI_type, comparator_15_eq, comparator_16_eq);
  and and_8 (SLTIU_type, comparator_17_eq, comparator_18_eq);
  Multiplexer multiplexer_33 (.in0(1'b0), .in1(1'b1), .out(multiplexer_33_out), .sel(ADD_type));
  Multiplexer multiplexer_34 (.in0(1'b0), .in1(1'b1), .out(multiplexer_34_out), .sel(SRA_type));
  Multiplexer multiplexer_35 (.in0(1'b0), .in1(1'b1), .out(multiplexer_35_out), .sel(SLT_type));
  Multiplexer multiplexer_36 (.in0(1'b0), .in1(1'b1), .out(multiplexer_36_out), .sel(SRLI_type));
  Multiplexer multiplexer_37 (.in0(1'b0), .in1(1'b1), .out(multiplexer_37_out), .sel(SLTIU_type));
  Multiplexer multiplexer_38 (.in0(1'b0), .in1(1'b1), .out(multiplexer_38_out), .sel(ANDI_type));
  Multiplexer multiplexer_39 (.in0(1'b0), .in1(1'b1), .out(multiplexer_39_out), .sel(ADDI_type));
  Multiplexer multiplexer_40 (.in0(1'b0), .in1(1'b1), .out(multiplexer_40_out), .sel(LW_type));
  Multiplexer multiplexer_41 (.in0(1'b0), .in1(1'b1), .out(multiplexer_41_out), .sel(LH_type));
  Multiplexer multiplexer_42 (.in0(1'b0), .in1(1'b1), .out(multiplexer_42_out), .sel(JALR_type));
  Multiplexer multiplexer_43 (.in0(1'b0), .in1(1'b1), .out(multiplexer_43_out), .sel(AUIPC_type));
  Multiplexer multiplexer_44 (.in0(1'b0), .in1(1'b1), .out(multiplexer_44_out), .sel(LUI_type));
  Multiplexer multiplexer_45 (.in0(1'b0), .in1(1'b0), .out(multiplexer_45_out), .sel(SW_type));
  Multiplexer multiplexer_46 (.in0(1'b0), .in1(1'b0), .out(multiplexer_46_out), .sel(SH_type));
  Multiplexer multiplexer_47 (.in0(1'b0), .in1(1'b1), .out(multiplexer_47_out), .sel(JAL_type));
  Multiplexer multiplexer_48 (.in0(1'b0), .in1(1'b0), .out(multiplexer_48_out), .sel(BEQ_type));
  assign inst_id = multiplexer_1_out | multiplexer_2_out | multiplexer_3_out | multiplexer_4_out | multiplexer_5_out | multiplexer_6_out | multiplexer_7_out | multiplexer_8_out | multiplexer_9_out | multiplexer_10_out | multiplexer_11_out | multiplexer_12_out | multiplexer_13_out | multiplexer_14_out | multiplexer_15_out | multiplexer_16_out;  // OR_Gate or_1, 4 bits wide
  Comparator #(.mode("unsigned"), .width(7)) comparator_19 (
    .a(Inst[6:0]), .b(7'b0010011), .eq(comparator_19_eq));  // open: gt, lt
  Comparator #(.mode("unsigned"), .width(3)) comparator_20 (
    .a(Inst[14:12]), .b(3'b111), .eq(comparator_20_eq));  // open: gt, lt
  Comparator #(.mode("unsigned"), .width(7)) comparator_21 (
    .a(Inst[6:0]), .b(7'b0010011), .eq(comparator_21_eq));  // open: gt, lt
  Comparator #(.mode("unsigned"), .width(3)) comparator_22 (
    .a(Inst[14:12]), .b(3'b101), .eq(comparator_22_eq));  // open: gt, lt
  Comparator #(.mode("unsigned"), .width(7)) comparator_23 (
    .a(Inst[6:0]), .b(7'b0110011), .eq(comparator_23_eq));  // open: gt, lt
  Comparator #(.mode("unsigned"), .width(3)) comparator_24 (
    .a(Inst[14:12]), .b(3'b000), .eq(comparator_24_eq));  // open: gt, lt
  Comparator #(.mode("unsigned"), .width(7)) comparator_25 (
    .a(Inst[6:0]), .b(7'b0110011), .eq(comparator_25_eq));  // open: gt, lt
  Comparator #(.mode("unsigned"), .width(3)) comparator_26 (
    .a(Inst[14:12]), .b(3'b101), .eq(comparator_26_eq));  // open: gt, lt
  Comparator #(.mode("unsigned"), .width(7)) comparator_27 (
    .a(Inst[6:0]), .b(7'b0110011), .eq(comparator_27_eq));  // open: gt, lt
  Comparator #(.mode("unsigned"), .width(3)) comparator_28 (
    .a(Inst[14:12]), .b(3'b010), .eq(comparator_28_eq));  // open: gt, lt
  Multiplexer multiplexer_49 (.in0(1'b0), .in1(1'b0), .out(multiplexer_49_out), .sel(ADD_type));
  Multiplexer multiplexer_50 (.in0(1'b0), .in1(1'b0), .out(multiplexer_50_out), .sel(SRA_type));
  Multiplexer multiplexer_51 (.in0(1'b0), .in1(1'b0), .out(multiplexer_51_out), .sel(SLT_type));
  Multiplexer multiplexer_52 (.in0(1'b0), .in1(1'b0), .out(multiplexer_52_out), .sel(SRLI_type));
  Multiplexer multiplexer_53 (.in0(1'b0), .in1(1'b0), .out(multiplexer_53_out), .sel(SLTIU_type));
  Multiplexer multiplexer_54 (.in0(1'b0), .in1(1'b0), .out(multiplexer_54_out), .sel(ANDI_type));
  Multiplexer multiplexer_55 (.in0(1'b0), .in1(1'b0), .out(multiplexer_55_out), .sel(ADDI_type));
  Multiplexer multiplexer_56 (.in0(1'b0), .in1(1'b0), .out(multiplexer_56_out), .sel(LW_type));
  Multiplexer multiplexer_57 (.in0(1'b0), .in1(1'b0), .out(multiplexer_57_out), .sel(LH_type));
  Multiplexer multiplexer_58 (.in0(1'b0), .in1(1'b0), .out(multiplexer_58_out), .sel(JALR_type));
  Multiplexer multiplexer_59 (.in0(1'b0), .in1(1'b0), .out(multiplexer_59_out), .sel(AUIPC_type));
  Multiplexer multiplexer_60 (.in0(1'b0), .in1(1'b0), .out(multiplexer_60_out), .sel(LUI_type));
  Multiplexer multiplexer_61 (.in0(1'b0), .in1(1'b1), .out(multiplexer_61_out), .sel(SW_type));
  Multiplexer multiplexer_62 (.in0(1'b0), .in1(1'b1), .out(multiplexer_62_out), .sel(SH_type));
  Multiplexer multiplexer_63 (.in0(1'b0), .in1(1'b0), .out(multiplexer_63_out), .sel(JAL_type));
  Multiplexer multiplexer_64 (.in0(1'b0), .in1(1'b0), .out(multiplexer_64_out), .sel(BEQ_type));
  or or_2 (PCsel, multiplexer_17_out, multiplexer_18_out, multiplexer_19_out, multiplexer_20_out, multiplexer_21_out, multiplexer_22_out, multiplexer_23_out, multiplexer_24_out, multiplexer_25_out, multiplexer_26_out, multiplexer_27_out, multiplexer_28_out, multiplexer_29_out, multiplexer_30_out, multiplexer_31_out, and_3_out);
  and and_9 (ANDI_type, comparator_19_eq, comparator_20_eq);
  and and_10 (SRLI_type, comparator_21_eq, comparator_22_eq);
  and and_11 (ADD_type, comparator_23_eq, comparator_24_eq);
  and and_12 (SRA_type, comparator_25_eq, comparator_26_eq);
  and and_13 (SLT_type, comparator_27_eq, comparator_28_eq);
  Multiplexer multiplexer_65 (.in0(1'b0), .in1(1'b0), .out(multiplexer_65_out), .sel(ADD_type));
  Multiplexer multiplexer_66 (.in0(1'b0), .in1(1'b0), .out(multiplexer_66_out), .sel(SRA_type));
  Multiplexer multiplexer_67 (.in0(1'b0), .in1(1'b0), .out(multiplexer_67_out), .sel(SLT_type));
  Multiplexer multiplexer_68 (.in0(1'b0), .in1(1'b0), .out(multiplexer_68_out), .sel(SRLI_type));
  Multiplexer multiplexer_69 (.in0(1'b0), .in1(1'b0), .out(multiplexer_69_out), .sel(SLTIU_type));
  Multiplexer multiplexer_70 (.in0(1'b0), .in1(1'b0), .out(multiplexer_70_out), .sel(ANDI_type));
  Multiplexer multiplexer_71 (.in0(1'b0), .in1(1'b0), .out(multiplexer_71_out), .sel(ADDI_type));
  Multiplexer multiplexer_72 (.in0(1'b0), .in1(1'b0), .out(multiplexer_72_out), .sel(LW_type));
  Multiplexer multiplexer_73 (.in0(1'b0), .in1(1'b0), .out(multiplexer_73_out), .sel(LH_type));
  Multiplexer multiplexer_74 (.in0(1'b0), .in1(1'b0), .out(multiplexer_74_out), .sel(JALR_type));
  Multiplexer multiplexer_75 (.in0(1'b0), .in1(1'b0), .out(multiplexer_75_out), .sel(AUIPC_type));
  Multiplexer multiplexer_76 (.in0(1'b0), .in1(1'b0), .out(multiplexer_76_out), .sel(LUI_type));
  Multiplexer multiplexer_77 (.in0(1'b0), .in1(1'b0), .out(multiplexer_77_out), .sel(SW_type));
  Multiplexer multiplexer_78 (.in0(1'b0), .in1(1'b1), .out(multiplexer_78_out), .sel(SH_type));
  Multiplexer multiplexer_79 (.in0(1'b0), .in1(1'b0), .out(multiplexer_79_out), .sel(JAL_type));
  Multiplexer multiplexer_80 (.in0(1'b0), .in1(1'b0), .out(multiplexer_80_out), .sel(BEQ_type));
  or or_3 (RegWEn, multiplexer_33_out, multiplexer_34_out, multiplexer_35_out, multiplexer_36_out, multiplexer_37_out, multiplexer_38_out, multiplexer_39_out, multiplexer_40_out, multiplexer_41_out, multiplexer_42_out, multiplexer_43_out, multiplexer_44_out, multiplexer_45_out, multiplexer_46_out, multiplexer_47_out, multiplexer_48_out);
  Multiplexer multiplexer_81 (.in0(1'b0), .in1(1'b0), .out(multiplexer_81_out), .sel(ADD_type));
  Multiplexer multiplexer_82 (.in0(1'b0), .in1(1'b0), .out(multiplexer_82_out), .sel(SRA_type));
  Multiplexer multiplexer_83 (.in0(1'b0), .in1(1'b0), .out(multiplexer_83_out), .sel(SLT_type));
  Multiplexer multiplexer_84 (.in0(1'b0), .in1(1'b0), .out(multiplexer_84_out), .sel(SRLI_type));
  Multiplexer multiplexer_85 (.in0(1'b0), .in1(1'b0), .out(multiplexer_85_out), .sel(SLTIU_type));
  Multiplexer multiplexer_86 (.in0(1'b0), .in1(1'b0), .out(multiplexer_86_out), .sel(ANDI_type));
  Multiplexer multiplexer_87 (.in0(1'b0), .in1(1'b0), .out(multiplexer_87_out), .sel(ADDI_type));
  Multiplexer multiplexer_88 (.in0(1'b0), .in1(1'b0), .out(multiplexer_88_out), .sel(LW_type));
  Multiplexer multiplexer_89 (.in0(1'b0), .in1(1'b1), .out(multiplexer_89_out), .sel(LH_type));
  Multiplexer multiplexer_90 (.in0(1'b0), .in1(1'b0), .out(multiplexer_90_out), .sel(JALR_type));
  Multiplexer multiplexer_91 (.in0(1'b0), .in1(1'b0), .out(multiplexer_91_out), .sel(AUIPC_type));
  Multiplexer multiplexer_92 (.in0(1'b0), .in1(1'b0), .out(multiplexer_92_out), .sel(LUI_type));
  Multiplexer multiplexer_93 (.in0(1'b0), .in1(1'b0), .out(multiplexer_93_out), .sel(SW_type));
  Multiplexer multiplexer_94 (.in0(1'b0), .in1(1'b0), .out(multiplexer_94_out), .sel(SH_type));
  Multiplexer multiplexer_95 (.in0(1'b0), .in1(1'b0), .out(multiplexer_95_out), .sel(JAL_type));
  Multiplexer multiplexer_96 (.in0(1'b0), .in1(1'b0), .out(multiplexer_96_out), .sel(BEQ_type));
  or or_4 (MemRW, multiplexer_49_out, multiplexer_50_out, multiplexer_51_out, multiplexer_52_out, multiplexer_53_out, multiplexer_54_out, multiplexer_55_out, multiplexer_56_out, multiplexer_57_out, multiplexer_58_out, multiplexer_59_out, multiplexer_60_out, multiplexer_61_out, multiplexer_62_out, multiplexer_63_out, multiplexer_64_out);
  Multiplexer multiplexer_97 (.in0(1'b0), .in1(1'b1), .out(multiplexer_97_out), .sel(ADD_type));
  Multiplexer multiplexer_98 (.in0(1'b0), .in1(1'b1), .out(multiplexer_98_out), .sel(SRA_type));
  Multiplexer multiplexer_99 (.in0(1'b0), .in1(1'b1), .out(multiplexer_99_out), .sel(SLT_type));
  Multiplexer multiplexer_100 (.in0(1'b0), .in1(1'b1), .out(multiplexer_100_out), .sel(SRLI_type));
  Multiplexer multiplexer_101 (.in0(1'b0), .in1(1'b1), .out(multiplexer_101_out), .sel(SLTIU_type));
  Multiplexer multiplexer_102 (.in0(1'b0), .in1(1'b1), .out(multiplexer_102_out), .sel(ANDI_type));
  Multiplexer multiplexer_103 (.in0(1'b0), .in1(1'b1), .out(multiplexer_103_out), .sel(ADDI_type));
  Multiplexer multiplexer_104 (.in0(1'b0), .in1(1'b0), .out(multiplexer_104_out), .sel(LW_type));
  Multiplexer multiplexer_105 (.in0(1'b0), .in1(1'b0), .out(multiplexer_105_out), .sel(LH_type));
  Multiplexer multiplexer_106 (.in0(1'b0), .in1(1'b1), .out(multiplexer_106_out), .sel(JALR_type));
  Multiplexer multiplexer_107 (.in0(1'b0), .in1(1'b1), .out(multiplexer_107_out), .sel(AUIPC_type));
  Multiplexer multiplexer_108 (.in0(1'b0), .in1(1'b1), .out(multiplexer_108_out), .sel(LUI_type));
  Multiplexer multiplexer_109 (.in0(1'b0), .in1(1'b1), .out(multiplexer_109_out), .sel(SW_type));
  Multiplexer multiplexer_110 (.in0(1'b0), .in1(1'b1), .out(multiplexer_110_out), .sel(SH_type));
  Multiplexer multiplexer_111 (.in0(1'b0), .in1(1'b1), .out(multiplexer_111_out), .sel(JAL_type));
  Multiplexer multiplexer_112 (.in0(1'b0), .in1(1'b1), .out(multiplexer_112_out), .sel(BEQ_type));
  or or_5 (Write_half, multiplexer_65_out, multiplexer_66_out, multiplexer_67_out, multiplexer_68_out, multiplexer_69_out, multiplexer_70_out, multiplexer_71_out, multiplexer_72_out, multiplexer_73_out, multiplexer_74_out, multiplexer_75_out, multiplexer_76_out, multiplexer_77_out, multiplexer_78_out, multiplexer_79_out, multiplexer_80_out);
  or or_6 (Read_half, multiplexer_81_out, multiplexer_82_out, multiplexer_83_out, multiplexer_84_out, multiplexer_85_out, multiplexer_86_out, multiplexer_87_out, multiplexer_88_out, multiplexer_89_out, multiplexer_90_out, multiplexer_91_out, multiplexer_92_out, multiplexer_93_out, multiplexer_94_out, multiplexer_95_out, multiplexer_96_out);
  or or_7 (WB_sel, multiplexer_97_out, multiplexer_98_out, multiplexer_99_out, multiplexer_100_out, multiplexer_101_out, multiplexer_102_out, multiplexer_103_out, multiplexer_104_out, multiplexer_105_out, multiplexer_106_out, multiplexer_107_out, multiplexer_108_out, multiplexer_109_out, multiplexer_110_out, multiplexer_111_out, multiplexer_112_out);

  // Other names for the same wires on the sheet: Opcode[6:0] = Inst[6:0]; Func3[2:0] = Inst[14:12]
endmodule

module Control_logic_stage2 (
  input  [31:0] Inst,
  output [3:0] inst_id
);

  wire ADD_type, ADDI_type, ANDI_type, AUIPC_type, BEQ_type, comparator_1_eq, comparator_2_eq,
       comparator_7_eq, comparator_8_eq, comparator_9_eq, comparator_10_eq, comparator_11_eq,
       comparator_12_eq, comparator_13_eq, comparator_14_eq, comparator_15_eq, comparator_16_eq,
       comparator_17_eq, comparator_18_eq, comparator_19_eq, comparator_20_eq, comparator_21_eq,
       comparator_22_eq, comparator_23_eq, comparator_24_eq, comparator_25_eq, comparator_26_eq,
       comparator_27_eq, comparator_28_eq, JAL_type, JALR_type, LH_type, LUI_type, LW_type, SH_type,
       SLT_type, SLTIU_type, SRA_type, SRLI_type, SW_type;
  wire [3:0] multiplexer_1_out, multiplexer_2_out, multiplexer_3_out, multiplexer_4_out, multiplexer_5_out,
       multiplexer_6_out, multiplexer_7_out, multiplexer_8_out, multiplexer_9_out, multiplexer_10_out,
       multiplexer_11_out, multiplexer_12_out, multiplexer_13_out, multiplexer_14_out, multiplexer_15_out,
       multiplexer_16_out;

  Comparator #(.mode("unsigned"), .width(7)) comparator_1 (
    .a(Inst[6:0]), .b(7'b0000011), .eq(comparator_1_eq));  // open: gt, lt
  Comparator #(.mode("unsigned"), .width(3)) comparator_2 (
    .a(Inst[14:12]), .b(3'b001), .eq(comparator_2_eq));  // open: gt, lt
  Multiplexer #(.width(4)) multiplexer_1 (.in0(4'b0000), .in1(4'b0000), .out(multiplexer_1_out), .sel(ADD_type));
  Multiplexer #(.width(4)) multiplexer_2 (.in0(4'b0000), .in1(4'b0001), .out(multiplexer_2_out), .sel(SRA_type));
  Multiplexer #(.width(4)) multiplexer_3 (.in0(4'b0000), .in1(4'b0010), .out(multiplexer_3_out), .sel(SLT_type));
  Multiplexer #(.width(4)) multiplexer_4 (.in0(4'b0000), .in1(4'b0011), .out(multiplexer_4_out), .sel(SRLI_type));
  Multiplexer #(.width(4)) multiplexer_5 (.in0(4'b0000), .in1(4'b0100), .out(multiplexer_5_out), .sel(SLTIU_type));
  Multiplexer #(.width(4)) multiplexer_6 (.in0(4'b0000), .in1(4'b0101), .out(multiplexer_6_out), .sel(ANDI_type));
  Multiplexer #(.width(4)) multiplexer_7 (.in0(4'b0000), .in1(4'b0110), .out(multiplexer_7_out), .sel(ADDI_type));
  Multiplexer #(.width(4)) multiplexer_8 (.in0(4'b0000), .in1(4'b0111), .out(multiplexer_8_out), .sel(LW_type));
  Multiplexer #(.width(4)) multiplexer_9 (.in0(4'b0000), .in1(4'b1000), .out(multiplexer_9_out), .sel(LH_type));
  Multiplexer #(.width(4)) multiplexer_10 (.in0(4'b0000), .in1(4'b1001), .out(multiplexer_10_out), .sel(JALR_type));
  Multiplexer #(.width(4)) multiplexer_11 (.in0(4'b0000), .in1(4'b1010), .out(multiplexer_11_out), .sel(AUIPC_type));
  Multiplexer #(.width(4)) multiplexer_12 (.in0(4'b0000), .in1(4'b1011), .out(multiplexer_12_out), .sel(LUI_type));
  Multiplexer #(.width(4)) multiplexer_13 (.in0(4'b0000), .in1(4'b1100), .out(multiplexer_13_out), .sel(SW_type));
  Multiplexer #(.width(4)) multiplexer_14 (.in0(4'b0000), .in1(4'b1101), .out(multiplexer_14_out), .sel(SH_type));
  Multiplexer #(.width(4)) multiplexer_15 (.in0(4'b0000), .in1(4'b1110), .out(multiplexer_15_out), .sel(JAL_type));
  Multiplexer #(.width(4)) multiplexer_16 (.in0(4'b0000), .in1(4'b1111), .out(multiplexer_16_out), .sel(BEQ_type));
  Comparator #(.mode("unsigned"), .width(7)) comparator_3 (
    .a(Inst[6:0]), .b(7'b0110111), .eq(LUI_type));  // open: gt, lt
  Comparator #(.mode("unsigned"), .width(7)) comparator_4 (
    .a(Inst[6:0]), .b(7'b0010111), .eq(AUIPC_type));  // open: gt, lt
  Comparator #(.mode("unsigned"), .width(7)) comparator_5 (
    .a(Inst[6:0]), .b(7'b1101111), .eq(JAL_type));  // open: gt, lt
  Comparator #(.mode("unsigned"), .width(7)) comparator_6 (
    .a(Inst[6:0]), .b(7'b1100111), .eq(JALR_type));  // open: gt, lt
  Comparator #(.mode("unsigned"), .width(7)) comparator_7 (
    .a(Inst[6:0]), .b(7'b1100011), .eq(comparator_7_eq));  // open: gt, lt
  Comparator #(.mode("unsigned"), .width(3)) comparator_8 (
    .a(Inst[14:12]), .b(3'b000), .eq(comparator_8_eq));  // open: gt, lt
  and and_1 (BEQ_type, comparator_7_eq, comparator_8_eq);
  and and_2 (LH_type, comparator_1_eq, comparator_2_eq);
  Comparator #(.mode("unsigned"), .width(7)) comparator_9 (
    .a(Inst[6:0]), .b(7'b0000011), .eq(comparator_9_eq));  // open: gt, lt
  Comparator #(.mode("unsigned"), .width(3)) comparator_10 (
    .a(Inst[14:12]), .b(3'b010), .eq(comparator_10_eq));  // open: gt, lt
  Comparator #(.mode("unsigned"), .width(7)) comparator_11 (
    .a(Inst[6:0]), .b(7'b0100011), .eq(comparator_11_eq));  // open: gt, lt
  Comparator #(.mode("unsigned"), .width(3)) comparator_12 (
    .a(Inst[14:12]), .b(3'b010), .eq(comparator_12_eq));  // open: gt, lt
  Comparator #(.mode("unsigned"), .width(7)) comparator_13 (
    .a(Inst[6:0]), .b(7'b0100011), .eq(comparator_13_eq));  // open: gt, lt
  Comparator #(.mode("unsigned"), .width(3)) comparator_14 (
    .a(Inst[14:12]), .b(3'b001), .eq(comparator_14_eq));  // open: gt, lt
  Comparator #(.mode("unsigned"), .width(7)) comparator_15 (
    .a(Inst[6:0]), .b(7'b0010011), .eq(comparator_15_eq));  // open: gt, lt
  Comparator #(.mode("unsigned"), .width(3)) comparator_16 (
    .a(Inst[14:12]), .b(3'b000), .eq(comparator_16_eq));  // open: gt, lt
  Comparator #(.mode("unsigned"), .width(7)) comparator_17 (
    .a(Inst[6:0]), .b(7'b0010011), .eq(comparator_17_eq));  // open: gt, lt
  Comparator #(.mode("unsigned"), .width(3)) comparator_18 (
    .a(Inst[14:12]), .b(3'b011), .eq(comparator_18_eq));  // open: gt, lt
  and and_3 (LW_type, comparator_9_eq, comparator_10_eq);
  and and_4 (SW_type, comparator_11_eq, comparator_12_eq);
  and and_5 (SH_type, comparator_13_eq, comparator_14_eq);
  and and_6 (ADDI_type, comparator_15_eq, comparator_16_eq);
  and and_7 (SLTIU_type, comparator_17_eq, comparator_18_eq);
  assign inst_id = multiplexer_1_out | multiplexer_2_out | multiplexer_3_out | multiplexer_4_out | multiplexer_5_out | multiplexer_6_out | multiplexer_7_out | multiplexer_8_out | multiplexer_9_out | multiplexer_10_out | multiplexer_11_out | multiplexer_12_out | multiplexer_13_out | multiplexer_14_out | multiplexer_15_out | multiplexer_16_out;  // OR_Gate or_1, 4 bits wide
  Comparator #(.mode("unsigned"), .width(7)) comparator_19 (
    .a(Inst[6:0]), .b(7'b0010011), .eq(comparator_19_eq));  // open: gt, lt
  Comparator #(.mode("unsigned"), .width(3)) comparator_20 (
    .a(Inst[14:12]), .b(3'b111), .eq(comparator_20_eq));  // open: gt, lt
  Comparator #(.mode("unsigned"), .width(7)) comparator_21 (
    .a(Inst[6:0]), .b(7'b0010011), .eq(comparator_21_eq));  // open: gt, lt
  Comparator #(.mode("unsigned"), .width(3)) comparator_22 (
    .a(Inst[14:12]), .b(3'b101), .eq(comparator_22_eq));  // open: gt, lt
  Comparator #(.mode("unsigned"), .width(7)) comparator_23 (
    .a(Inst[6:0]), .b(7'b0110011), .eq(comparator_23_eq));  // open: gt, lt
  Comparator #(.mode("unsigned"), .width(3)) comparator_24 (
    .a(Inst[14:12]), .b(3'b000), .eq(comparator_24_eq));  // open: gt, lt
  Comparator #(.mode("unsigned"), .width(7)) comparator_25 (
    .a(Inst[6:0]), .b(7'b0110011), .eq(comparator_25_eq));  // open: gt, lt
  Comparator #(.mode("unsigned"), .width(3)) comparator_26 (
    .a(Inst[14:12]), .b(3'b101), .eq(comparator_26_eq));  // open: gt, lt
  Comparator #(.mode("unsigned"), .width(7)) comparator_27 (
    .a(Inst[6:0]), .b(7'b0110011), .eq(comparator_27_eq));  // open: gt, lt
  Comparator #(.mode("unsigned"), .width(3)) comparator_28 (
    .a(Inst[14:12]), .b(3'b010), .eq(comparator_28_eq));  // open: gt, lt
  and and_8 (ANDI_type, comparator_19_eq, comparator_20_eq);
  and and_9 (SRLI_type, comparator_21_eq, comparator_22_eq);
  and and_10 (ADD_type, comparator_23_eq, comparator_24_eq);
  and and_11 (SRA_type, comparator_25_eq, comparator_26_eq);
  and and_12 (SLT_type, comparator_27_eq, comparator_28_eq);

  // Other names for the same wires on the sheet: Opcode[6:0] = Inst[6:0]; Func3[2:0] = Inst[14:12]
endmodule

module Control_logic_stage4 (
  input  [31:0] Inst,
  output [3:0] inst_id,
  output WB_sel,
  output MemRW,
  output Write_half,
  output Read_half
);

  wire ADD_type, ADDI_type, and_3_out, ANDI_type, AUIPC_type, BEQ_type, comparator_1_eq, comparator_2_eq,
       comparator_7_eq, comparator_8_eq, comparator_9_eq, comparator_10_eq, comparator_11_eq,
       comparator_12_eq, comparator_13_eq, comparator_14_eq, comparator_15_eq, comparator_16_eq,
       comparator_17_eq, comparator_18_eq, comparator_19_eq, comparator_20_eq, comparator_21_eq,
       comparator_22_eq, comparator_23_eq, comparator_24_eq, comparator_25_eq, comparator_26_eq,
       comparator_27_eq, comparator_28_eq, Is_equal, JAL_type, JALR_type, LH_type, LUI_type, LW_type,
       multiplexer_17_out, multiplexer_18_out, multiplexer_19_out, multiplexer_20_out, multiplexer_21_out,
       multiplexer_22_out, multiplexer_23_out, multiplexer_24_out, multiplexer_25_out, multiplexer_26_out,
       multiplexer_27_out, multiplexer_28_out, multiplexer_29_out, multiplexer_30_out, multiplexer_31_out,
       multiplexer_32_out, multiplexer_33_out, multiplexer_34_out, multiplexer_35_out, multiplexer_36_out,
       multiplexer_37_out, multiplexer_38_out, multiplexer_39_out, multiplexer_40_out, multiplexer_41_out,
       multiplexer_42_out, multiplexer_43_out, multiplexer_44_out, multiplexer_45_out, multiplexer_46_out,
       multiplexer_47_out, multiplexer_48_out, multiplexer_49_out, multiplexer_50_out, multiplexer_51_out,
       multiplexer_52_out, multiplexer_53_out, multiplexer_54_out, multiplexer_55_out, multiplexer_56_out,
       multiplexer_57_out, multiplexer_58_out, multiplexer_59_out, multiplexer_60_out, multiplexer_61_out,
       multiplexer_62_out, multiplexer_63_out, multiplexer_64_out, multiplexer_65_out, multiplexer_66_out,
       multiplexer_67_out, multiplexer_68_out, multiplexer_69_out, multiplexer_70_out, multiplexer_71_out,
       multiplexer_72_out, multiplexer_73_out, multiplexer_74_out, multiplexer_75_out, multiplexer_76_out,
       multiplexer_77_out, multiplexer_78_out, multiplexer_79_out, multiplexer_80_out, multiplexer_81_out,
       multiplexer_82_out, multiplexer_83_out, multiplexer_84_out, multiplexer_85_out, multiplexer_86_out,
       multiplexer_87_out, multiplexer_88_out, multiplexer_89_out, multiplexer_90_out, multiplexer_91_out,
       multiplexer_92_out, multiplexer_93_out, multiplexer_94_out, multiplexer_95_out, multiplexer_96_out,
       multiplexer_97_out, multiplexer_98_out, multiplexer_99_out, multiplexer_100_out, multiplexer_101_out,
       multiplexer_102_out, multiplexer_103_out, multiplexer_104_out, multiplexer_105_out,
       multiplexer_106_out, multiplexer_107_out, multiplexer_108_out, multiplexer_109_out,
       multiplexer_110_out, multiplexer_111_out, multiplexer_112_out, PCsel, RegWEn, SH_type, SLT_type,
       SLTIU_type, SRA_type, SRLI_type, SW_type;
  wire [3:0] multiplexer_1_out, multiplexer_2_out, multiplexer_3_out, multiplexer_4_out, multiplexer_5_out,
       multiplexer_6_out, multiplexer_7_out, multiplexer_8_out, multiplexer_9_out, multiplexer_10_out,
       multiplexer_11_out, multiplexer_12_out, multiplexer_13_out, multiplexer_14_out, multiplexer_15_out,
       multiplexer_16_out;

  Comparator #(.mode("unsigned"), .width(7)) comparator_1 (
    .a(Inst[6:0]), .b(7'b0000011), .eq(comparator_1_eq));  // open: gt, lt
  Comparator #(.mode("unsigned"), .width(3)) comparator_2 (
    .a(Inst[14:12]), .b(3'b001), .eq(comparator_2_eq));  // open: gt, lt
  Multiplexer #(.width(4)) multiplexer_1 (.in0(4'b0000), .in1(4'b0000), .out(multiplexer_1_out), .sel(ADD_type));
  Multiplexer #(.width(4)) multiplexer_2 (.in0(4'b0000), .in1(4'b0001), .out(multiplexer_2_out), .sel(SRA_type));
  Multiplexer #(.width(4)) multiplexer_3 (.in0(4'b0000), .in1(4'b0010), .out(multiplexer_3_out), .sel(SLT_type));
  Multiplexer #(.width(4)) multiplexer_4 (.in0(4'b0000), .in1(4'b0011), .out(multiplexer_4_out), .sel(SRLI_type));
  Multiplexer #(.width(4)) multiplexer_5 (.in0(4'b0000), .in1(4'b0100), .out(multiplexer_5_out), .sel(SLTIU_type));
  Multiplexer #(.width(4)) multiplexer_6 (.in0(4'b0000), .in1(4'b0101), .out(multiplexer_6_out), .sel(ANDI_type));
  Multiplexer #(.width(4)) multiplexer_7 (.in0(4'b0000), .in1(4'b0110), .out(multiplexer_7_out), .sel(ADDI_type));
  Multiplexer #(.width(4)) multiplexer_8 (.in0(4'b0000), .in1(4'b0111), .out(multiplexer_8_out), .sel(LW_type));
  Multiplexer #(.width(4)) multiplexer_9 (.in0(4'b0000), .in1(4'b1000), .out(multiplexer_9_out), .sel(LH_type));
  Multiplexer #(.width(4)) multiplexer_10 (.in0(4'b0000), .in1(4'b1001), .out(multiplexer_10_out), .sel(JALR_type));
  Multiplexer #(.width(4)) multiplexer_11 (.in0(4'b0000), .in1(4'b1010), .out(multiplexer_11_out), .sel(AUIPC_type));
  Multiplexer #(.width(4)) multiplexer_12 (.in0(4'b0000), .in1(4'b1011), .out(multiplexer_12_out), .sel(LUI_type));
  Multiplexer #(.width(4)) multiplexer_13 (.in0(4'b0000), .in1(4'b1100), .out(multiplexer_13_out), .sel(SW_type));
  Multiplexer #(.width(4)) multiplexer_14 (.in0(4'b0000), .in1(4'b1101), .out(multiplexer_14_out), .sel(SH_type));
  Multiplexer #(.width(4)) multiplexer_15 (.in0(4'b0000), .in1(4'b1110), .out(multiplexer_15_out), .sel(JAL_type));
  Multiplexer #(.width(4)) multiplexer_16 (.in0(4'b0000), .in1(4'b1111), .out(multiplexer_16_out), .sel(BEQ_type));
  Comparator #(.mode("unsigned"), .width(7)) comparator_3 (
    .a(Inst[6:0]), .b(7'b0110111), .eq(LUI_type));  // open: gt, lt
  Comparator #(.mode("unsigned"), .width(7)) comparator_4 (
    .a(Inst[6:0]), .b(7'b0010111), .eq(AUIPC_type));  // open: gt, lt
  Comparator #(.mode("unsigned"), .width(7)) comparator_5 (
    .a(Inst[6:0]), .b(7'b1101111), .eq(JAL_type));  // open: gt, lt
  Comparator #(.mode("unsigned"), .width(7)) comparator_6 (
    .a(Inst[6:0]), .b(7'b1100111), .eq(JALR_type));  // open: gt, lt
  Comparator #(.mode("unsigned"), .width(7)) comparator_7 (
    .a(Inst[6:0]), .b(7'b1100011), .eq(comparator_7_eq));  // open: gt, lt
  Comparator #(.mode("unsigned"), .width(3)) comparator_8 (
    .a(Inst[14:12]), .b(3'b000), .eq(comparator_8_eq));  // open: gt, lt
  and and_1 (BEQ_type, comparator_7_eq, comparator_8_eq);
  and and_2 (LH_type, comparator_1_eq, comparator_2_eq);
  Multiplexer multiplexer_17 (.in0(1'b0), .in1(1'b0), .out(multiplexer_17_out), .sel(ADD_type));
  Multiplexer multiplexer_18 (.in0(1'b0), .in1(1'b0), .out(multiplexer_18_out), .sel(SRA_type));
  Multiplexer multiplexer_19 (.in0(1'b0), .in1(1'b0), .out(multiplexer_19_out), .sel(SLT_type));
  Multiplexer multiplexer_20 (.in0(1'b0), .in1(1'b0), .out(multiplexer_20_out), .sel(SRLI_type));
  Multiplexer multiplexer_21 (.in0(1'b0), .in1(1'b0), .out(multiplexer_21_out), .sel(SLTIU_type));
  Multiplexer multiplexer_22 (.in0(1'b0), .in1(1'b0), .out(multiplexer_22_out), .sel(ANDI_type));
  Multiplexer multiplexer_23 (.in0(1'b0), .in1(1'b0), .out(multiplexer_23_out), .sel(ADDI_type));
  Multiplexer multiplexer_24 (.in0(1'b0), .in1(1'b0), .out(multiplexer_24_out), .sel(LW_type));
  Multiplexer multiplexer_25 (.in0(1'b0), .in1(1'b0), .out(multiplexer_25_out), .sel(LH_type));
  Multiplexer multiplexer_26 (.in0(1'b0), .in1(1'b1), .out(multiplexer_26_out), .sel(JALR_type));
  Multiplexer multiplexer_27 (.in0(1'b0), .in1(1'b0), .out(multiplexer_27_out), .sel(AUIPC_type));
  Multiplexer multiplexer_28 (.in0(1'b0), .in1(1'b0), .out(multiplexer_28_out), .sel(LUI_type));
  Multiplexer multiplexer_29 (.in0(1'b0), .in1(1'b0), .out(multiplexer_29_out), .sel(SW_type));
  Multiplexer multiplexer_30 (.in0(1'b0), .in1(1'b0), .out(multiplexer_30_out), .sel(SH_type));
  Multiplexer multiplexer_31 (.in0(1'b0), .in1(1'b1), .out(multiplexer_31_out), .sel(JAL_type));
  Multiplexer multiplexer_32 (.in0(1'b0), .in1(1'b1), .out(multiplexer_32_out), .sel(BEQ_type));
  Comparator #(.mode("unsigned"), .width(7)) comparator_9 (
    .a(Inst[6:0]), .b(7'b0000011), .eq(comparator_9_eq));  // open: gt, lt
  Comparator #(.mode("unsigned"), .width(3)) comparator_10 (
    .a(Inst[14:12]), .b(3'b010), .eq(comparator_10_eq));  // open: gt, lt
  Comparator #(.mode("unsigned"), .width(7)) comparator_11 (
    .a(Inst[6:0]), .b(7'b0100011), .eq(comparator_11_eq));  // open: gt, lt
  Comparator #(.mode("unsigned"), .width(3)) comparator_12 (
    .a(Inst[14:12]), .b(3'b010), .eq(comparator_12_eq));  // open: gt, lt
  Comparator #(.mode("unsigned"), .width(7)) comparator_13 (
    .a(Inst[6:0]), .b(7'b0100011), .eq(comparator_13_eq));  // open: gt, lt
  Comparator #(.mode("unsigned"), .width(3)) comparator_14 (
    .a(Inst[14:12]), .b(3'b001), .eq(comparator_14_eq));  // open: gt, lt
  Comparator #(.mode("unsigned"), .width(7)) comparator_15 (
    .a(Inst[6:0]), .b(7'b0010011), .eq(comparator_15_eq));  // open: gt, lt
  Comparator #(.mode("unsigned"), .width(3)) comparator_16 (
    .a(Inst[14:12]), .b(3'b000), .eq(comparator_16_eq));  // open: gt, lt
  Comparator #(.mode("unsigned"), .width(7)) comparator_17 (
    .a(Inst[6:0]), .b(7'b0010011), .eq(comparator_17_eq));  // open: gt, lt
  Comparator #(.mode("unsigned"), .width(3)) comparator_18 (
    .a(Inst[14:12]), .b(3'b011), .eq(comparator_18_eq));  // open: gt, lt
  and and_3 (and_3_out, multiplexer_32_out, Is_equal);
  and and_4 (LW_type, comparator_9_eq, comparator_10_eq);
  and and_5 (SW_type, comparator_11_eq, comparator_12_eq);
  and and_6 (SH_type, comparator_13_eq, comparator_14_eq);
  and and_7 (ADDI_type, comparator_15_eq, comparator_16_eq);
  and and_8 (SLTIU_type, comparator_17_eq, comparator_18_eq);
  Multiplexer multiplexer_33 (.in0(1'b0), .in1(1'b1), .out(multiplexer_33_out), .sel(ADD_type));
  Multiplexer multiplexer_34 (.in0(1'b0), .in1(1'b1), .out(multiplexer_34_out), .sel(SRA_type));
  Multiplexer multiplexer_35 (.in0(1'b0), .in1(1'b1), .out(multiplexer_35_out), .sel(SLT_type));
  Multiplexer multiplexer_36 (.in0(1'b0), .in1(1'b1), .out(multiplexer_36_out), .sel(SRLI_type));
  Multiplexer multiplexer_37 (.in0(1'b0), .in1(1'b1), .out(multiplexer_37_out), .sel(SLTIU_type));
  Multiplexer multiplexer_38 (.in0(1'b0), .in1(1'b1), .out(multiplexer_38_out), .sel(ANDI_type));
  Multiplexer multiplexer_39 (.in0(1'b0), .in1(1'b1), .out(multiplexer_39_out), .sel(ADDI_type));
  Multiplexer multiplexer_40 (.in0(1'b0), .in1(1'b1), .out(multiplexer_40_out), .sel(LW_type));
  Multiplexer multiplexer_41 (.in0(1'b0), .in1(1'b1), .out(multiplexer_41_out), .sel(LH_type));
  Multiplexer multiplexer_42 (.in0(1'b0), .in1(1'b1), .out(multiplexer_42_out), .sel(JALR_type));
  Multiplexer multiplexer_43 (.in0(1'b0), .in1(1'b1), .out(multiplexer_43_out), .sel(AUIPC_type));
  Multiplexer multiplexer_44 (.in0(1'b0), .in1(1'b1), .out(multiplexer_44_out), .sel(LUI_type));
  Multiplexer multiplexer_45 (.in0(1'b0), .in1(1'b0), .out(multiplexer_45_out), .sel(SW_type));
  Multiplexer multiplexer_46 (.in0(1'b0), .in1(1'b0), .out(multiplexer_46_out), .sel(SH_type));
  Multiplexer multiplexer_47 (.in0(1'b0), .in1(1'b1), .out(multiplexer_47_out), .sel(JAL_type));
  Multiplexer multiplexer_48 (.in0(1'b0), .in1(1'b0), .out(multiplexer_48_out), .sel(BEQ_type));
  assign inst_id = multiplexer_1_out | multiplexer_2_out | multiplexer_3_out | multiplexer_4_out | multiplexer_5_out | multiplexer_6_out | multiplexer_7_out | multiplexer_8_out | multiplexer_9_out | multiplexer_10_out | multiplexer_11_out | multiplexer_12_out | multiplexer_13_out | multiplexer_14_out | multiplexer_15_out | multiplexer_16_out;  // OR_Gate or_1, 4 bits wide
  Comparator #(.mode("unsigned"), .width(7)) comparator_19 (
    .a(Inst[6:0]), .b(7'b0010011), .eq(comparator_19_eq));  // open: gt, lt
  Comparator #(.mode("unsigned"), .width(3)) comparator_20 (
    .a(Inst[14:12]), .b(3'b111), .eq(comparator_20_eq));  // open: gt, lt
  Comparator #(.mode("unsigned"), .width(7)) comparator_21 (
    .a(Inst[6:0]), .b(7'b0010011), .eq(comparator_21_eq));  // open: gt, lt
  Comparator #(.mode("unsigned"), .width(3)) comparator_22 (
    .a(Inst[14:12]), .b(3'b101), .eq(comparator_22_eq));  // open: gt, lt
  Comparator #(.mode("unsigned"), .width(7)) comparator_23 (
    .a(Inst[6:0]), .b(7'b0110011), .eq(comparator_23_eq));  // open: gt, lt
  Comparator #(.mode("unsigned"), .width(3)) comparator_24 (
    .a(Inst[14:12]), .b(3'b000), .eq(comparator_24_eq));  // open: gt, lt
  Comparator #(.mode("unsigned"), .width(7)) comparator_25 (
    .a(Inst[6:0]), .b(7'b0110011), .eq(comparator_25_eq));  // open: gt, lt
  Comparator #(.mode("unsigned"), .width(3)) comparator_26 (
    .a(Inst[14:12]), .b(3'b101), .eq(comparator_26_eq));  // open: gt, lt
  Comparator #(.mode("unsigned"), .width(7)) comparator_27 (
    .a(Inst[6:0]), .b(7'b0110011), .eq(comparator_27_eq));  // open: gt, lt
  Comparator #(.mode("unsigned"), .width(3)) comparator_28 (
    .a(Inst[14:12]), .b(3'b010), .eq(comparator_28_eq));  // open: gt, lt
  Multiplexer multiplexer_49 (.in0(1'b0), .in1(1'b0), .out(multiplexer_49_out), .sel(ADD_type));
  Multiplexer multiplexer_50 (.in0(1'b0), .in1(1'b0), .out(multiplexer_50_out), .sel(SRA_type));
  Multiplexer multiplexer_51 (.in0(1'b0), .in1(1'b0), .out(multiplexer_51_out), .sel(SLT_type));
  Multiplexer multiplexer_52 (.in0(1'b0), .in1(1'b0), .out(multiplexer_52_out), .sel(SRLI_type));
  Multiplexer multiplexer_53 (.in0(1'b0), .in1(1'b0), .out(multiplexer_53_out), .sel(SLTIU_type));
  Multiplexer multiplexer_54 (.in0(1'b0), .in1(1'b0), .out(multiplexer_54_out), .sel(ANDI_type));
  Multiplexer multiplexer_55 (.in0(1'b0), .in1(1'b0), .out(multiplexer_55_out), .sel(ADDI_type));
  Multiplexer multiplexer_56 (.in0(1'b0), .in1(1'b0), .out(multiplexer_56_out), .sel(LW_type));
  Multiplexer multiplexer_57 (.in0(1'b0), .in1(1'b0), .out(multiplexer_57_out), .sel(LH_type));
  Multiplexer multiplexer_58 (.in0(1'b0), .in1(1'b0), .out(multiplexer_58_out), .sel(JALR_type));
  Multiplexer multiplexer_59 (.in0(1'b0), .in1(1'b0), .out(multiplexer_59_out), .sel(AUIPC_type));
  Multiplexer multiplexer_60 (.in0(1'b0), .in1(1'b0), .out(multiplexer_60_out), .sel(LUI_type));
  Multiplexer multiplexer_61 (.in0(1'b0), .in1(1'b1), .out(multiplexer_61_out), .sel(SW_type));
  Multiplexer multiplexer_62 (.in0(1'b0), .in1(1'b1), .out(multiplexer_62_out), .sel(SH_type));
  Multiplexer multiplexer_63 (.in0(1'b0), .in1(1'b0), .out(multiplexer_63_out), .sel(JAL_type));
  Multiplexer multiplexer_64 (.in0(1'b0), .in1(1'b0), .out(multiplexer_64_out), .sel(BEQ_type));
  or or_2 (PCsel, multiplexer_17_out, multiplexer_18_out, multiplexer_19_out, multiplexer_20_out, multiplexer_21_out, multiplexer_22_out, multiplexer_23_out, multiplexer_24_out, multiplexer_25_out, multiplexer_26_out, multiplexer_27_out, multiplexer_28_out, multiplexer_29_out, multiplexer_30_out, multiplexer_31_out, and_3_out);
  and and_9 (ANDI_type, comparator_19_eq, comparator_20_eq);
  and and_10 (SRLI_type, comparator_21_eq, comparator_22_eq);
  and and_11 (ADD_type, comparator_23_eq, comparator_24_eq);
  and and_12 (SRA_type, comparator_25_eq, comparator_26_eq);
  and and_13 (SLT_type, comparator_27_eq, comparator_28_eq);
  Multiplexer multiplexer_65 (.in0(1'b0), .in1(1'b0), .out(multiplexer_65_out), .sel(ADD_type));
  Multiplexer multiplexer_66 (.in0(1'b0), .in1(1'b0), .out(multiplexer_66_out), .sel(SRA_type));
  Multiplexer multiplexer_67 (.in0(1'b0), .in1(1'b0), .out(multiplexer_67_out), .sel(SLT_type));
  Multiplexer multiplexer_68 (.in0(1'b0), .in1(1'b0), .out(multiplexer_68_out), .sel(SRLI_type));
  Multiplexer multiplexer_69 (.in0(1'b0), .in1(1'b0), .out(multiplexer_69_out), .sel(SLTIU_type));
  Multiplexer multiplexer_70 (.in0(1'b0), .in1(1'b0), .out(multiplexer_70_out), .sel(ANDI_type));
  Multiplexer multiplexer_71 (.in0(1'b0), .in1(1'b0), .out(multiplexer_71_out), .sel(ADDI_type));
  Multiplexer multiplexer_72 (.in0(1'b0), .in1(1'b0), .out(multiplexer_72_out), .sel(LW_type));
  Multiplexer multiplexer_73 (.in0(1'b0), .in1(1'b0), .out(multiplexer_73_out), .sel(LH_type));
  Multiplexer multiplexer_74 (.in0(1'b0), .in1(1'b0), .out(multiplexer_74_out), .sel(JALR_type));
  Multiplexer multiplexer_75 (.in0(1'b0), .in1(1'b0), .out(multiplexer_75_out), .sel(AUIPC_type));
  Multiplexer multiplexer_76 (.in0(1'b0), .in1(1'b0), .out(multiplexer_76_out), .sel(LUI_type));
  Multiplexer multiplexer_77 (.in0(1'b0), .in1(1'b0), .out(multiplexer_77_out), .sel(SW_type));
  Multiplexer multiplexer_78 (.in0(1'b0), .in1(1'b1), .out(multiplexer_78_out), .sel(SH_type));
  Multiplexer multiplexer_79 (.in0(1'b0), .in1(1'b0), .out(multiplexer_79_out), .sel(JAL_type));
  Multiplexer multiplexer_80 (.in0(1'b0), .in1(1'b0), .out(multiplexer_80_out), .sel(BEQ_type));
  or or_3 (RegWEn, multiplexer_33_out, multiplexer_34_out, multiplexer_35_out, multiplexer_36_out, multiplexer_37_out, multiplexer_38_out, multiplexer_39_out, multiplexer_40_out, multiplexer_41_out, multiplexer_42_out, multiplexer_43_out, multiplexer_44_out, multiplexer_45_out, multiplexer_46_out, multiplexer_47_out, multiplexer_48_out);
  Multiplexer multiplexer_81 (.in0(1'b0), .in1(1'b0), .out(multiplexer_81_out), .sel(ADD_type));
  Multiplexer multiplexer_82 (.in0(1'b0), .in1(1'b0), .out(multiplexer_82_out), .sel(SRA_type));
  Multiplexer multiplexer_83 (.in0(1'b0), .in1(1'b0), .out(multiplexer_83_out), .sel(SLT_type));
  Multiplexer multiplexer_84 (.in0(1'b0), .in1(1'b0), .out(multiplexer_84_out), .sel(SRLI_type));
  Multiplexer multiplexer_85 (.in0(1'b0), .in1(1'b0), .out(multiplexer_85_out), .sel(SLTIU_type));
  Multiplexer multiplexer_86 (.in0(1'b0), .in1(1'b0), .out(multiplexer_86_out), .sel(ANDI_type));
  Multiplexer multiplexer_87 (.in0(1'b0), .in1(1'b0), .out(multiplexer_87_out), .sel(ADDI_type));
  Multiplexer multiplexer_88 (.in0(1'b0), .in1(1'b0), .out(multiplexer_88_out), .sel(LW_type));
  Multiplexer multiplexer_89 (.in0(1'b0), .in1(1'b1), .out(multiplexer_89_out), .sel(LH_type));
  Multiplexer multiplexer_90 (.in0(1'b0), .in1(1'b0), .out(multiplexer_90_out), .sel(JALR_type));
  Multiplexer multiplexer_91 (.in0(1'b0), .in1(1'b0), .out(multiplexer_91_out), .sel(AUIPC_type));
  Multiplexer multiplexer_92 (.in0(1'b0), .in1(1'b0), .out(multiplexer_92_out), .sel(LUI_type));
  Multiplexer multiplexer_93 (.in0(1'b0), .in1(1'b0), .out(multiplexer_93_out), .sel(SW_type));
  Multiplexer multiplexer_94 (.in0(1'b0), .in1(1'b0), .out(multiplexer_94_out), .sel(SH_type));
  Multiplexer multiplexer_95 (.in0(1'b0), .in1(1'b0), .out(multiplexer_95_out), .sel(JAL_type));
  Multiplexer multiplexer_96 (.in0(1'b0), .in1(1'b0), .out(multiplexer_96_out), .sel(BEQ_type));
  or or_4 (MemRW, multiplexer_49_out, multiplexer_50_out, multiplexer_51_out, multiplexer_52_out, multiplexer_53_out, multiplexer_54_out, multiplexer_55_out, multiplexer_56_out, multiplexer_57_out, multiplexer_58_out, multiplexer_59_out, multiplexer_60_out, multiplexer_61_out, multiplexer_62_out, multiplexer_63_out, multiplexer_64_out);
  Multiplexer multiplexer_97 (.in0(1'b0), .in1(1'b1), .out(multiplexer_97_out), .sel(ADD_type));
  Multiplexer multiplexer_98 (.in0(1'b0), .in1(1'b1), .out(multiplexer_98_out), .sel(SRA_type));
  Multiplexer multiplexer_99 (.in0(1'b0), .in1(1'b1), .out(multiplexer_99_out), .sel(SLT_type));
  Multiplexer multiplexer_100 (.in0(1'b0), .in1(1'b1), .out(multiplexer_100_out), .sel(SRLI_type));
  Multiplexer multiplexer_101 (.in0(1'b0), .in1(1'b1), .out(multiplexer_101_out), .sel(SLTIU_type));
  Multiplexer multiplexer_102 (.in0(1'b0), .in1(1'b1), .out(multiplexer_102_out), .sel(ANDI_type));
  Multiplexer multiplexer_103 (.in0(1'b0), .in1(1'b1), .out(multiplexer_103_out), .sel(ADDI_type));
  Multiplexer multiplexer_104 (.in0(1'b0), .in1(1'b0), .out(multiplexer_104_out), .sel(LW_type));
  Multiplexer multiplexer_105 (.in0(1'b0), .in1(1'b0), .out(multiplexer_105_out), .sel(LH_type));
  Multiplexer multiplexer_106 (.in0(1'b0), .in1(1'b1), .out(multiplexer_106_out), .sel(JALR_type));
  Multiplexer multiplexer_107 (.in0(1'b0), .in1(1'b1), .out(multiplexer_107_out), .sel(AUIPC_type));
  Multiplexer multiplexer_108 (.in0(1'b0), .in1(1'b1), .out(multiplexer_108_out), .sel(LUI_type));
  Multiplexer multiplexer_109 (.in0(1'b0), .in1(1'b1), .out(multiplexer_109_out), .sel(SW_type));
  Multiplexer multiplexer_110 (.in0(1'b0), .in1(1'b1), .out(multiplexer_110_out), .sel(SH_type));
  Multiplexer multiplexer_111 (.in0(1'b0), .in1(1'b1), .out(multiplexer_111_out), .sel(JAL_type));
  Multiplexer multiplexer_112 (.in0(1'b0), .in1(1'b1), .out(multiplexer_112_out), .sel(BEQ_type));
  or or_5 (Write_half, multiplexer_65_out, multiplexer_66_out, multiplexer_67_out, multiplexer_68_out, multiplexer_69_out, multiplexer_70_out, multiplexer_71_out, multiplexer_72_out, multiplexer_73_out, multiplexer_74_out, multiplexer_75_out, multiplexer_76_out, multiplexer_77_out, multiplexer_78_out, multiplexer_79_out, multiplexer_80_out);
  or or_6 (Read_half, multiplexer_81_out, multiplexer_82_out, multiplexer_83_out, multiplexer_84_out, multiplexer_85_out, multiplexer_86_out, multiplexer_87_out, multiplexer_88_out, multiplexer_89_out, multiplexer_90_out, multiplexer_91_out, multiplexer_92_out, multiplexer_93_out, multiplexer_94_out, multiplexer_95_out, multiplexer_96_out);
  or or_7 (WB_sel, multiplexer_97_out, multiplexer_98_out, multiplexer_99_out, multiplexer_100_out, multiplexer_101_out, multiplexer_102_out, multiplexer_103_out, multiplexer_104_out, multiplexer_105_out, multiplexer_106_out, multiplexer_107_out, multiplexer_108_out, multiplexer_109_out, multiplexer_110_out, multiplexer_111_out, multiplexer_112_out);

  // Other names for the same wires on the sheet: Opcode[6:0] = Inst[6:0]; Func3[2:0] = Inst[14:12]
endmodule
module Control_logic_stage3 (
  input  [31:0] Inst,
  output [3:0] inst_id
);

  wire ADD_type, ADDI_type, and_3_out, ANDI_type, AUIPC_type, BEQ_type, comparator_1_eq, comparator_2_eq,
       comparator_7_eq, comparator_8_eq, comparator_9_eq, comparator_10_eq, comparator_11_eq,
       comparator_12_eq, comparator_13_eq, comparator_14_eq, comparator_15_eq, comparator_16_eq,
       comparator_17_eq, comparator_18_eq, comparator_19_eq, comparator_20_eq, comparator_21_eq,
       comparator_22_eq, comparator_23_eq, comparator_24_eq, comparator_25_eq, comparator_26_eq,
       comparator_27_eq, comparator_28_eq, Is_equal, JAL_type, JALR_type, LH_type, LUI_type, LW_type, MemRW,
       multiplexer_17_out, multiplexer_18_out, multiplexer_19_out, multiplexer_20_out, multiplexer_21_out,
       multiplexer_22_out, multiplexer_23_out, multiplexer_24_out, multiplexer_25_out, multiplexer_26_out,
       multiplexer_27_out, multiplexer_28_out, multiplexer_29_out, multiplexer_30_out, multiplexer_31_out,
       multiplexer_32_out, multiplexer_33_out, multiplexer_34_out, multiplexer_35_out, multiplexer_36_out,
       multiplexer_37_out, multiplexer_38_out, multiplexer_39_out, multiplexer_40_out, multiplexer_41_out,
       multiplexer_42_out, multiplexer_43_out, multiplexer_44_out, multiplexer_45_out, multiplexer_46_out,
       multiplexer_47_out, multiplexer_48_out, multiplexer_49_out, multiplexer_50_out, multiplexer_51_out,
       multiplexer_52_out, multiplexer_53_out, multiplexer_54_out, multiplexer_55_out, multiplexer_56_out,
       multiplexer_57_out, multiplexer_58_out, multiplexer_59_out, multiplexer_60_out, multiplexer_61_out,
       multiplexer_62_out, multiplexer_63_out, multiplexer_64_out, multiplexer_65_out, multiplexer_66_out,
       multiplexer_67_out, multiplexer_68_out, multiplexer_69_out, multiplexer_70_out, multiplexer_71_out,
       multiplexer_72_out, multiplexer_73_out, multiplexer_74_out, multiplexer_75_out, multiplexer_76_out,
       multiplexer_77_out, multiplexer_78_out, multiplexer_79_out, multiplexer_80_out, multiplexer_81_out,
       multiplexer_82_out, multiplexer_83_out, multiplexer_84_out, multiplexer_85_out, multiplexer_86_out,
       multiplexer_87_out, multiplexer_88_out, multiplexer_89_out, multiplexer_90_out, multiplexer_91_out,
       multiplexer_92_out, multiplexer_93_out, multiplexer_94_out, multiplexer_95_out, multiplexer_96_out,
       multiplexer_97_out, multiplexer_98_out, multiplexer_99_out, multiplexer_100_out, multiplexer_101_out,
       multiplexer_102_out, multiplexer_103_out, multiplexer_104_out, multiplexer_105_out,
       multiplexer_106_out, multiplexer_107_out, multiplexer_108_out, multiplexer_109_out,
       multiplexer_110_out, multiplexer_111_out, multiplexer_112_out, PCsel, Read_half, RegWEn, SH_type,
       SLT_type, SLTIU_type, SRA_type, SRLI_type, SW_type, WB_sel, Write_half;
  wire [3:0] multiplexer_1_out, multiplexer_2_out, multiplexer_3_out, multiplexer_4_out, multiplexer_5_out,
       multiplexer_6_out, multiplexer_7_out, multiplexer_8_out, multiplexer_9_out, multiplexer_10_out,
       multiplexer_11_out, multiplexer_12_out, multiplexer_13_out, multiplexer_14_out, multiplexer_15_out,
       multiplexer_16_out;

  Comparator #(.mode("unsigned"), .width(7)) comparator_1 (
    .a(Inst[6:0]), .b(7'b0000011), .eq(comparator_1_eq));  // open: gt, lt
  Comparator #(.mode("unsigned"), .width(3)) comparator_2 (
    .a(Inst[14:12]), .b(3'b001), .eq(comparator_2_eq));  // open: gt, lt
  Multiplexer #(.width(4)) multiplexer_1 (.in0(4'b0000), .in1(4'b0000), .out(multiplexer_1_out), .sel(ADD_type));
  Multiplexer #(.width(4)) multiplexer_2 (.in0(4'b0000), .in1(4'b0001), .out(multiplexer_2_out), .sel(SRA_type));
  Multiplexer #(.width(4)) multiplexer_3 (.in0(4'b0000), .in1(4'b0010), .out(multiplexer_3_out), .sel(SLT_type));
  Multiplexer #(.width(4)) multiplexer_4 (.in0(4'b0000), .in1(4'b0011), .out(multiplexer_4_out), .sel(SRLI_type));
  Multiplexer #(.width(4)) multiplexer_5 (.in0(4'b0000), .in1(4'b0100), .out(multiplexer_5_out), .sel(SLTIU_type));
  Multiplexer #(.width(4)) multiplexer_6 (.in0(4'b0000), .in1(4'b0101), .out(multiplexer_6_out), .sel(ANDI_type));
  Multiplexer #(.width(4)) multiplexer_7 (.in0(4'b0000), .in1(4'b0110), .out(multiplexer_7_out), .sel(ADDI_type));
  Multiplexer #(.width(4)) multiplexer_8 (.in0(4'b0000), .in1(4'b0111), .out(multiplexer_8_out), .sel(LW_type));
  Multiplexer #(.width(4)) multiplexer_9 (.in0(4'b0000), .in1(4'b1000), .out(multiplexer_9_out), .sel(LH_type));
  Multiplexer #(.width(4)) multiplexer_10 (.in0(4'b0000), .in1(4'b1001), .out(multiplexer_10_out), .sel(JALR_type));
  Multiplexer #(.width(4)) multiplexer_11 (.in0(4'b0000), .in1(4'b1010), .out(multiplexer_11_out), .sel(AUIPC_type));
  Multiplexer #(.width(4)) multiplexer_12 (.in0(4'b0000), .in1(4'b1011), .out(multiplexer_12_out), .sel(LUI_type));
  Multiplexer #(.width(4)) multiplexer_13 (.in0(4'b0000), .in1(4'b1100), .out(multiplexer_13_out), .sel(SW_type));
  Multiplexer #(.width(4)) multiplexer_14 (.in0(4'b0000), .in1(4'b1101), .out(multiplexer_14_out), .sel(SH_type));
  Multiplexer #(.width(4)) multiplexer_15 (.in0(4'b0000), .in1(4'b1110), .out(multiplexer_15_out), .sel(JAL_type));
  Multiplexer #(.width(4)) multiplexer_16 (.in0(4'b0000), .in1(4'b1111), .out(multiplexer_16_out), .sel(BEQ_type));
  Comparator #(.mode("unsigned"), .width(7)) comparator_3 (
    .a(Inst[6:0]), .b(7'b0110111), .eq(LUI_type));  // open: gt, lt
  Comparator #(.mode("unsigned"), .width(7)) comparator_4 (
    .a(Inst[6:0]), .b(7'b0010111), .eq(AUIPC_type));  // open: gt, lt
  Comparator #(.mode("unsigned"), .width(7)) comparator_5 (
    .a(Inst[6:0]), .b(7'b1101111), .eq(JAL_type));  // open: gt, lt
  Comparator #(.mode("unsigned"), .width(7)) comparator_6 (
    .a(Inst[6:0]), .b(7'b1100111), .eq(JALR_type));  // open: gt, lt
  Comparator #(.mode("unsigned"), .width(7)) comparator_7 (
    .a(Inst[6:0]), .b(7'b1100011), .eq(comparator_7_eq));  // open: gt, lt
  Comparator #(.mode("unsigned"), .width(3)) comparator_8 (
    .a(Inst[14:12]), .b(3'b000), .eq(comparator_8_eq));  // open: gt, lt
  and and_1 (BEQ_type, comparator_7_eq, comparator_8_eq);
  and and_2 (LH_type, comparator_1_eq, comparator_2_eq);
  Multiplexer multiplexer_17 (.in0(1'b0), .in1(1'b0), .out(multiplexer_17_out), .sel(ADD_type));
  Multiplexer multiplexer_18 (.in0(1'b0), .in1(1'b0), .out(multiplexer_18_out), .sel(SRA_type));
  Multiplexer multiplexer_19 (.in0(1'b0), .in1(1'b0), .out(multiplexer_19_out), .sel(SLT_type));
  Multiplexer multiplexer_20 (.in0(1'b0), .in1(1'b0), .out(multiplexer_20_out), .sel(SRLI_type));
  Multiplexer multiplexer_21 (.in0(1'b0), .in1(1'b0), .out(multiplexer_21_out), .sel(SLTIU_type));
  Multiplexer multiplexer_22 (.in0(1'b0), .in1(1'b0), .out(multiplexer_22_out), .sel(ANDI_type));
  Multiplexer multiplexer_23 (.in0(1'b0), .in1(1'b0), .out(multiplexer_23_out), .sel(ADDI_type));
  Multiplexer multiplexer_24 (.in0(1'b0), .in1(1'b0), .out(multiplexer_24_out), .sel(LW_type));
  Multiplexer multiplexer_25 (.in0(1'b0), .in1(1'b0), .out(multiplexer_25_out), .sel(LH_type));
  Multiplexer multiplexer_26 (.in0(1'b0), .in1(1'b1), .out(multiplexer_26_out), .sel(JALR_type));
  Multiplexer multiplexer_27 (.in0(1'b0), .in1(1'b0), .out(multiplexer_27_out), .sel(AUIPC_type));
  Multiplexer multiplexer_28 (.in0(1'b0), .in1(1'b0), .out(multiplexer_28_out), .sel(LUI_type));
  Multiplexer multiplexer_29 (.in0(1'b0), .in1(1'b0), .out(multiplexer_29_out), .sel(SW_type));
  Multiplexer multiplexer_30 (.in0(1'b0), .in1(1'b0), .out(multiplexer_30_out), .sel(SH_type));
  Multiplexer multiplexer_31 (.in0(1'b0), .in1(1'b1), .out(multiplexer_31_out), .sel(JAL_type));
  Multiplexer multiplexer_32 (.in0(1'b0), .in1(1'b1), .out(multiplexer_32_out), .sel(BEQ_type));
  Comparator #(.mode("unsigned"), .width(7)) comparator_9 (
    .a(Inst[6:0]), .b(7'b0000011), .eq(comparator_9_eq));  // open: gt, lt
  Comparator #(.mode("unsigned"), .width(3)) comparator_10 (
    .a(Inst[14:12]), .b(3'b010), .eq(comparator_10_eq));  // open: gt, lt
  Comparator #(.mode("unsigned"), .width(7)) comparator_11 (
    .a(Inst[6:0]), .b(7'b0100011), .eq(comparator_11_eq));  // open: gt, lt
  Comparator #(.mode("unsigned"), .width(3)) comparator_12 (
    .a(Inst[14:12]), .b(3'b010), .eq(comparator_12_eq));  // open: gt, lt
  Comparator #(.mode("unsigned"), .width(7)) comparator_13 (
    .a(Inst[6:0]), .b(7'b0100011), .eq(comparator_13_eq));  // open: gt, lt
  Comparator #(.mode("unsigned"), .width(3)) comparator_14 (
    .a(Inst[14:12]), .b(3'b001), .eq(comparator_14_eq));  // open: gt, lt
  Comparator #(.mode("unsigned"), .width(7)) comparator_15 (
    .a(Inst[6:0]), .b(7'b0010011), .eq(comparator_15_eq));  // open: gt, lt
  Comparator #(.mode("unsigned"), .width(3)) comparator_16 (
    .a(Inst[14:12]), .b(3'b000), .eq(comparator_16_eq));  // open: gt, lt
  Comparator #(.mode("unsigned"), .width(7)) comparator_17 (
    .a(Inst[6:0]), .b(7'b0010011), .eq(comparator_17_eq));  // open: gt, lt
  Comparator #(.mode("unsigned"), .width(3)) comparator_18 (
    .a(Inst[14:12]), .b(3'b011), .eq(comparator_18_eq));  // open: gt, lt
  and and_3 (and_3_out, multiplexer_32_out, Is_equal);
  and and_4 (LW_type, comparator_9_eq, comparator_10_eq);
  and and_5 (SW_type, comparator_11_eq, comparator_12_eq);
  and and_6 (SH_type, comparator_13_eq, comparator_14_eq);
  and and_7 (ADDI_type, comparator_15_eq, comparator_16_eq);
  and and_8 (SLTIU_type, comparator_17_eq, comparator_18_eq);
  Multiplexer multiplexer_33 (.in0(1'b0), .in1(1'b1), .out(multiplexer_33_out), .sel(ADD_type));
  Multiplexer multiplexer_34 (.in0(1'b0), .in1(1'b1), .out(multiplexer_34_out), .sel(SRA_type));
  Multiplexer multiplexer_35 (.in0(1'b0), .in1(1'b1), .out(multiplexer_35_out), .sel(SLT_type));
  Multiplexer multiplexer_36 (.in0(1'b0), .in1(1'b1), .out(multiplexer_36_out), .sel(SRLI_type));
  Multiplexer multiplexer_37 (.in0(1'b0), .in1(1'b1), .out(multiplexer_37_out), .sel(SLTIU_type));
  Multiplexer multiplexer_38 (.in0(1'b0), .in1(1'b1), .out(multiplexer_38_out), .sel(ANDI_type));
  Multiplexer multiplexer_39 (.in0(1'b0), .in1(1'b1), .out(multiplexer_39_out), .sel(ADDI_type));
  Multiplexer multiplexer_40 (.in0(1'b0), .in1(1'b1), .out(multiplexer_40_out), .sel(LW_type));
  Multiplexer multiplexer_41 (.in0(1'b0), .in1(1'b1), .out(multiplexer_41_out), .sel(LH_type));
  Multiplexer multiplexer_42 (.in0(1'b0), .in1(1'b1), .out(multiplexer_42_out), .sel(JALR_type));
  Multiplexer multiplexer_43 (.in0(1'b0), .in1(1'b1), .out(multiplexer_43_out), .sel(AUIPC_type));
  Multiplexer multiplexer_44 (.in0(1'b0), .in1(1'b1), .out(multiplexer_44_out), .sel(LUI_type));
  Multiplexer multiplexer_45 (.in0(1'b0), .in1(1'b0), .out(multiplexer_45_out), .sel(SW_type));
  Multiplexer multiplexer_46 (.in0(1'b0), .in1(1'b0), .out(multiplexer_46_out), .sel(SH_type));
  Multiplexer multiplexer_47 (.in0(1'b0), .in1(1'b1), .out(multiplexer_47_out), .sel(JAL_type));
  Multiplexer multiplexer_48 (.in0(1'b0), .in1(1'b0), .out(multiplexer_48_out), .sel(BEQ_type));
  assign inst_id = multiplexer_1_out | multiplexer_2_out | multiplexer_3_out | multiplexer_4_out | multiplexer_5_out | multiplexer_6_out | multiplexer_7_out | multiplexer_8_out | multiplexer_9_out | multiplexer_10_out | multiplexer_11_out | multiplexer_12_out | multiplexer_13_out | multiplexer_14_out | multiplexer_15_out | multiplexer_16_out;  // OR_Gate or_1, 4 bits wide
  Comparator #(.mode("unsigned"), .width(7)) comparator_19 (
    .a(Inst[6:0]), .b(7'b0010011), .eq(comparator_19_eq));  // open: gt, lt
  Comparator #(.mode("unsigned"), .width(3)) comparator_20 (
    .a(Inst[14:12]), .b(3'b111), .eq(comparator_20_eq));  // open: gt, lt
  Comparator #(.mode("unsigned"), .width(7)) comparator_21 (
    .a(Inst[6:0]), .b(7'b0010011), .eq(comparator_21_eq));  // open: gt, lt
  Comparator #(.mode("unsigned"), .width(3)) comparator_22 (
    .a(Inst[14:12]), .b(3'b101), .eq(comparator_22_eq));  // open: gt, lt
  Comparator #(.mode("unsigned"), .width(7)) comparator_23 (
    .a(Inst[6:0]), .b(7'b0110011), .eq(comparator_23_eq));  // open: gt, lt
  Comparator #(.mode("unsigned"), .width(3)) comparator_24 (
    .a(Inst[14:12]), .b(3'b000), .eq(comparator_24_eq));  // open: gt, lt
  Comparator #(.mode("unsigned"), .width(7)) comparator_25 (
    .a(Inst[6:0]), .b(7'b0110011), .eq(comparator_25_eq));  // open: gt, lt
  Comparator #(.mode("unsigned"), .width(3)) comparator_26 (
    .a(Inst[14:12]), .b(3'b101), .eq(comparator_26_eq));  // open: gt, lt
  Comparator #(.mode("unsigned"), .width(7)) comparator_27 (
    .a(Inst[6:0]), .b(7'b0110011), .eq(comparator_27_eq));  // open: gt, lt
  Comparator #(.mode("unsigned"), .width(3)) comparator_28 (
    .a(Inst[14:12]), .b(3'b010), .eq(comparator_28_eq));  // open: gt, lt
  Multiplexer multiplexer_49 (.in0(1'b0), .in1(1'b0), .out(multiplexer_49_out), .sel(ADD_type));
  Multiplexer multiplexer_50 (.in0(1'b0), .in1(1'b0), .out(multiplexer_50_out), .sel(SRA_type));
  Multiplexer multiplexer_51 (.in0(1'b0), .in1(1'b0), .out(multiplexer_51_out), .sel(SLT_type));
  Multiplexer multiplexer_52 (.in0(1'b0), .in1(1'b0), .out(multiplexer_52_out), .sel(SRLI_type));
  Multiplexer multiplexer_53 (.in0(1'b0), .in1(1'b0), .out(multiplexer_53_out), .sel(SLTIU_type));
  Multiplexer multiplexer_54 (.in0(1'b0), .in1(1'b0), .out(multiplexer_54_out), .sel(ANDI_type));
  Multiplexer multiplexer_55 (.in0(1'b0), .in1(1'b0), .out(multiplexer_55_out), .sel(ADDI_type));
  Multiplexer multiplexer_56 (.in0(1'b0), .in1(1'b0), .out(multiplexer_56_out), .sel(LW_type));
  Multiplexer multiplexer_57 (.in0(1'b0), .in1(1'b0), .out(multiplexer_57_out), .sel(LH_type));
  Multiplexer multiplexer_58 (.in0(1'b0), .in1(1'b0), .out(multiplexer_58_out), .sel(JALR_type));
  Multiplexer multiplexer_59 (.in0(1'b0), .in1(1'b0), .out(multiplexer_59_out), .sel(AUIPC_type));
  Multiplexer multiplexer_60 (.in0(1'b0), .in1(1'b0), .out(multiplexer_60_out), .sel(LUI_type));
  Multiplexer multiplexer_61 (.in0(1'b0), .in1(1'b1), .out(multiplexer_61_out), .sel(SW_type));
  Multiplexer multiplexer_62 (.in0(1'b0), .in1(1'b1), .out(multiplexer_62_out), .sel(SH_type));
  Multiplexer multiplexer_63 (.in0(1'b0), .in1(1'b0), .out(multiplexer_63_out), .sel(JAL_type));
  Multiplexer multiplexer_64 (.in0(1'b0), .in1(1'b0), .out(multiplexer_64_out), .sel(BEQ_type));
  or or_2 (PCsel, multiplexer_17_out, multiplexer_18_out, multiplexer_19_out, multiplexer_20_out, multiplexer_21_out, multiplexer_22_out, multiplexer_23_out, multiplexer_24_out, multiplexer_25_out, multiplexer_26_out, multiplexer_27_out, multiplexer_28_out, multiplexer_29_out, multiplexer_30_out, multiplexer_31_out, and_3_out);
  and and_9 (ANDI_type, comparator_19_eq, comparator_20_eq);
  and and_10 (SRLI_type, comparator_21_eq, comparator_22_eq);
  and and_11 (ADD_type, comparator_23_eq, comparator_24_eq);
  and and_12 (SRA_type, comparator_25_eq, comparator_26_eq);
  and and_13 (SLT_type, comparator_27_eq, comparator_28_eq);
  Multiplexer multiplexer_65 (.in0(1'b0), .in1(1'b0), .out(multiplexer_65_out), .sel(ADD_type));
  Multiplexer multiplexer_66 (.in0(1'b0), .in1(1'b0), .out(multiplexer_66_out), .sel(SRA_type));
  Multiplexer multiplexer_67 (.in0(1'b0), .in1(1'b0), .out(multiplexer_67_out), .sel(SLT_type));
  Multiplexer multiplexer_68 (.in0(1'b0), .in1(1'b0), .out(multiplexer_68_out), .sel(SRLI_type));
  Multiplexer multiplexer_69 (.in0(1'b0), .in1(1'b0), .out(multiplexer_69_out), .sel(SLTIU_type));
  Multiplexer multiplexer_70 (.in0(1'b0), .in1(1'b0), .out(multiplexer_70_out), .sel(ANDI_type));
  Multiplexer multiplexer_71 (.in0(1'b0), .in1(1'b0), .out(multiplexer_71_out), .sel(ADDI_type));
  Multiplexer multiplexer_72 (.in0(1'b0), .in1(1'b0), .out(multiplexer_72_out), .sel(LW_type));
  Multiplexer multiplexer_73 (.in0(1'b0), .in1(1'b0), .out(multiplexer_73_out), .sel(LH_type));
  Multiplexer multiplexer_74 (.in0(1'b0), .in1(1'b0), .out(multiplexer_74_out), .sel(JALR_type));
  Multiplexer multiplexer_75 (.in0(1'b0), .in1(1'b0), .out(multiplexer_75_out), .sel(AUIPC_type));
  Multiplexer multiplexer_76 (.in0(1'b0), .in1(1'b0), .out(multiplexer_76_out), .sel(LUI_type));
  Multiplexer multiplexer_77 (.in0(1'b0), .in1(1'b0), .out(multiplexer_77_out), .sel(SW_type));
  Multiplexer multiplexer_78 (.in0(1'b0), .in1(1'b1), .out(multiplexer_78_out), .sel(SH_type));
  Multiplexer multiplexer_79 (.in0(1'b0), .in1(1'b0), .out(multiplexer_79_out), .sel(JAL_type));
  Multiplexer multiplexer_80 (.in0(1'b0), .in1(1'b0), .out(multiplexer_80_out), .sel(BEQ_type));
  or or_3 (RegWEn, multiplexer_33_out, multiplexer_34_out, multiplexer_35_out, multiplexer_36_out, multiplexer_37_out, multiplexer_38_out, multiplexer_39_out, multiplexer_40_out, multiplexer_41_out, multiplexer_42_out, multiplexer_43_out, multiplexer_44_out, multiplexer_45_out, multiplexer_46_out, multiplexer_47_out, multiplexer_48_out);
  Multiplexer multiplexer_81 (.in0(1'b0), .in1(1'b0), .out(multiplexer_81_out), .sel(ADD_type));
  Multiplexer multiplexer_82 (.in0(1'b0), .in1(1'b0), .out(multiplexer_82_out), .sel(SRA_type));
  Multiplexer multiplexer_83 (.in0(1'b0), .in1(1'b0), .out(multiplexer_83_out), .sel(SLT_type));
  Multiplexer multiplexer_84 (.in0(1'b0), .in1(1'b0), .out(multiplexer_84_out), .sel(SRLI_type));
  Multiplexer multiplexer_85 (.in0(1'b0), .in1(1'b0), .out(multiplexer_85_out), .sel(SLTIU_type));
  Multiplexer multiplexer_86 (.in0(1'b0), .in1(1'b0), .out(multiplexer_86_out), .sel(ANDI_type));
  Multiplexer multiplexer_87 (.in0(1'b0), .in1(1'b0), .out(multiplexer_87_out), .sel(ADDI_type));
  Multiplexer multiplexer_88 (.in0(1'b0), .in1(1'b0), .out(multiplexer_88_out), .sel(LW_type));
  Multiplexer multiplexer_89 (.in0(1'b0), .in1(1'b1), .out(multiplexer_89_out), .sel(LH_type));
  Multiplexer multiplexer_90 (.in0(1'b0), .in1(1'b0), .out(multiplexer_90_out), .sel(JALR_type));
  Multiplexer multiplexer_91 (.in0(1'b0), .in1(1'b0), .out(multiplexer_91_out), .sel(AUIPC_type));
  Multiplexer multiplexer_92 (.in0(1'b0), .in1(1'b0), .out(multiplexer_92_out), .sel(LUI_type));
  Multiplexer multiplexer_93 (.in0(1'b0), .in1(1'b0), .out(multiplexer_93_out), .sel(SW_type));
  Multiplexer multiplexer_94 (.in0(1'b0), .in1(1'b0), .out(multiplexer_94_out), .sel(SH_type));
  Multiplexer multiplexer_95 (.in0(1'b0), .in1(1'b0), .out(multiplexer_95_out), .sel(JAL_type));
  Multiplexer multiplexer_96 (.in0(1'b0), .in1(1'b0), .out(multiplexer_96_out), .sel(BEQ_type));
  or or_4 (MemRW, multiplexer_49_out, multiplexer_50_out, multiplexer_51_out, multiplexer_52_out, multiplexer_53_out, multiplexer_54_out, multiplexer_55_out, multiplexer_56_out, multiplexer_57_out, multiplexer_58_out, multiplexer_59_out, multiplexer_60_out, multiplexer_61_out, multiplexer_62_out, multiplexer_63_out, multiplexer_64_out);
  Multiplexer multiplexer_97 (.in0(1'b0), .in1(1'b1), .out(multiplexer_97_out), .sel(ADD_type));
  Multiplexer multiplexer_98 (.in0(1'b0), .in1(1'b1), .out(multiplexer_98_out), .sel(SRA_type));
  Multiplexer multiplexer_99 (.in0(1'b0), .in1(1'b1), .out(multiplexer_99_out), .sel(SLT_type));
  Multiplexer multiplexer_100 (.in0(1'b0), .in1(1'b1), .out(multiplexer_100_out), .sel(SRLI_type));
  Multiplexer multiplexer_101 (.in0(1'b0), .in1(1'b1), .out(multiplexer_101_out), .sel(SLTIU_type));
  Multiplexer multiplexer_102 (.in0(1'b0), .in1(1'b1), .out(multiplexer_102_out), .sel(ANDI_type));
  Multiplexer multiplexer_103 (.in0(1'b0), .in1(1'b1), .out(multiplexer_103_out), .sel(ADDI_type));
  Multiplexer multiplexer_104 (.in0(1'b0), .in1(1'b0), .out(multiplexer_104_out), .sel(LW_type));
  Multiplexer multiplexer_105 (.in0(1'b0), .in1(1'b0), .out(multiplexer_105_out), .sel(LH_type));
  Multiplexer multiplexer_106 (.in0(1'b0), .in1(1'b1), .out(multiplexer_106_out), .sel(JALR_type));
  Multiplexer multiplexer_107 (.in0(1'b0), .in1(1'b1), .out(multiplexer_107_out), .sel(AUIPC_type));
  Multiplexer multiplexer_108 (.in0(1'b0), .in1(1'b1), .out(multiplexer_108_out), .sel(LUI_type));
  Multiplexer multiplexer_109 (.in0(1'b0), .in1(1'b1), .out(multiplexer_109_out), .sel(SW_type));
  Multiplexer multiplexer_110 (.in0(1'b0), .in1(1'b1), .out(multiplexer_110_out), .sel(SH_type));
  Multiplexer multiplexer_111 (.in0(1'b0), .in1(1'b1), .out(multiplexer_111_out), .sel(JAL_type));
  Multiplexer multiplexer_112 (.in0(1'b0), .in1(1'b1), .out(multiplexer_112_out), .sel(BEQ_type));
  or or_5 (Write_half, multiplexer_65_out, multiplexer_66_out, multiplexer_67_out, multiplexer_68_out, multiplexer_69_out, multiplexer_70_out, multiplexer_71_out, multiplexer_72_out, multiplexer_73_out, multiplexer_74_out, multiplexer_75_out, multiplexer_76_out, multiplexer_77_out, multiplexer_78_out, multiplexer_79_out, multiplexer_80_out);
  or or_6 (Read_half, multiplexer_81_out, multiplexer_82_out, multiplexer_83_out, multiplexer_84_out, multiplexer_85_out, multiplexer_86_out, multiplexer_87_out, multiplexer_88_out, multiplexer_89_out, multiplexer_90_out, multiplexer_91_out, multiplexer_92_out, multiplexer_93_out, multiplexer_94_out, multiplexer_95_out, multiplexer_96_out);
  or or_7 (WB_sel, multiplexer_97_out, multiplexer_98_out, multiplexer_99_out, multiplexer_100_out, multiplexer_101_out, multiplexer_102_out, multiplexer_103_out, multiplexer_104_out, multiplexer_105_out, multiplexer_106_out, multiplexer_107_out, multiplexer_108_out, multiplexer_109_out, multiplexer_110_out, multiplexer_111_out, multiplexer_112_out);

  // Other names for the same wires on the sheet: Opcode[6:0] = Inst[6:0]; Func3[2:0] = Inst[14:12]
endmodule

module Control_logic_stage5 (
  input  [31:0] Inst,
  output RegWEn,
  output [3:0] inst_id
);

  wire ADD_type, ADDI_type, and_3_out, ANDI_type, AUIPC_type, BEQ_type, comparator_1_eq, comparator_2_eq,
       comparator_7_eq, comparator_8_eq, comparator_9_eq, comparator_10_eq, comparator_11_eq,
       comparator_12_eq, comparator_13_eq, comparator_14_eq, comparator_15_eq, comparator_16_eq,
       comparator_17_eq, comparator_18_eq, comparator_19_eq, comparator_20_eq, comparator_21_eq,
       comparator_22_eq, comparator_23_eq, comparator_24_eq, comparator_25_eq, comparator_26_eq,
       comparator_27_eq, comparator_28_eq, Is_equal, JAL_type, JALR_type, LH_type, LUI_type, LW_type, MemRW,
       multiplexer_17_out, multiplexer_18_out, multiplexer_19_out, multiplexer_20_out, multiplexer_21_out,
       multiplexer_22_out, multiplexer_23_out, multiplexer_24_out, multiplexer_25_out, multiplexer_26_out,
       multiplexer_27_out, multiplexer_28_out, multiplexer_29_out, multiplexer_30_out, multiplexer_31_out,
       multiplexer_32_out, multiplexer_33_out, multiplexer_34_out, multiplexer_35_out, multiplexer_36_out,
       multiplexer_37_out, multiplexer_38_out, multiplexer_39_out, multiplexer_40_out, multiplexer_41_out,
       multiplexer_42_out, multiplexer_43_out, multiplexer_44_out, multiplexer_45_out, multiplexer_46_out,
       multiplexer_47_out, multiplexer_48_out, multiplexer_49_out, multiplexer_50_out, multiplexer_51_out,
       multiplexer_52_out, multiplexer_53_out, multiplexer_54_out, multiplexer_55_out, multiplexer_56_out,
       multiplexer_57_out, multiplexer_58_out, multiplexer_59_out, multiplexer_60_out, multiplexer_61_out,
       multiplexer_62_out, multiplexer_63_out, multiplexer_64_out, multiplexer_65_out, multiplexer_66_out,
       multiplexer_67_out, multiplexer_68_out, multiplexer_69_out, multiplexer_70_out, multiplexer_71_out,
       multiplexer_72_out, multiplexer_73_out, multiplexer_74_out, multiplexer_75_out, multiplexer_76_out,
       multiplexer_77_out, multiplexer_78_out, multiplexer_79_out, multiplexer_80_out, multiplexer_81_out,
       multiplexer_82_out, multiplexer_83_out, multiplexer_84_out, multiplexer_85_out, multiplexer_86_out,
       multiplexer_87_out, multiplexer_88_out, multiplexer_89_out, multiplexer_90_out, multiplexer_91_out,
       multiplexer_92_out, multiplexer_93_out, multiplexer_94_out, multiplexer_95_out, multiplexer_96_out,
       multiplexer_97_out, multiplexer_98_out, multiplexer_99_out, multiplexer_100_out, multiplexer_101_out,
       multiplexer_102_out, multiplexer_103_out, multiplexer_104_out, multiplexer_105_out,
       multiplexer_106_out, multiplexer_107_out, multiplexer_108_out, multiplexer_109_out,
       multiplexer_110_out, multiplexer_111_out, multiplexer_112_out, PCsel, Read_half, SH_type, SLT_type,
       SLTIU_type, SRA_type, SRLI_type, SW_type, WB_sel, Write_half;
  wire [3:0] multiplexer_1_out, multiplexer_2_out, multiplexer_3_out, multiplexer_4_out, multiplexer_5_out,
       multiplexer_6_out, multiplexer_7_out, multiplexer_8_out, multiplexer_9_out, multiplexer_10_out,
       multiplexer_11_out, multiplexer_12_out, multiplexer_13_out, multiplexer_14_out, multiplexer_15_out,
       multiplexer_16_out;

  Comparator #(.mode("unsigned"), .width(7)) comparator_1 (
    .a(Inst[6:0]), .b(7'b0000011), .eq(comparator_1_eq));  // open: gt, lt
  Comparator #(.mode("unsigned"), .width(3)) comparator_2 (
    .a(Inst[14:12]), .b(3'b001), .eq(comparator_2_eq));  // open: gt, lt
  Multiplexer #(.width(4)) multiplexer_1 (.in0(4'b0000), .in1(4'b0000), .out(multiplexer_1_out), .sel(ADD_type));
  Multiplexer #(.width(4)) multiplexer_2 (.in0(4'b0000), .in1(4'b0001), .out(multiplexer_2_out), .sel(SRA_type));
  Multiplexer #(.width(4)) multiplexer_3 (.in0(4'b0000), .in1(4'b0010), .out(multiplexer_3_out), .sel(SLT_type));
  Multiplexer #(.width(4)) multiplexer_4 (.in0(4'b0000), .in1(4'b0011), .out(multiplexer_4_out), .sel(SRLI_type));
  Multiplexer #(.width(4)) multiplexer_5 (.in0(4'b0000), .in1(4'b0100), .out(multiplexer_5_out), .sel(SLTIU_type));
  Multiplexer #(.width(4)) multiplexer_6 (.in0(4'b0000), .in1(4'b0101), .out(multiplexer_6_out), .sel(ANDI_type));
  Multiplexer #(.width(4)) multiplexer_7 (.in0(4'b0000), .in1(4'b0110), .out(multiplexer_7_out), .sel(ADDI_type));
  Multiplexer #(.width(4)) multiplexer_8 (.in0(4'b0000), .in1(4'b0111), .out(multiplexer_8_out), .sel(LW_type));
  Multiplexer #(.width(4)) multiplexer_9 (.in0(4'b0000), .in1(4'b1000), .out(multiplexer_9_out), .sel(LH_type));
  Multiplexer #(.width(4)) multiplexer_10 (.in0(4'b0000), .in1(4'b1001), .out(multiplexer_10_out), .sel(JALR_type));
  Multiplexer #(.width(4)) multiplexer_11 (.in0(4'b0000), .in1(4'b1010), .out(multiplexer_11_out), .sel(AUIPC_type));
  Multiplexer #(.width(4)) multiplexer_12 (.in0(4'b0000), .in1(4'b1011), .out(multiplexer_12_out), .sel(LUI_type));
  Multiplexer #(.width(4)) multiplexer_13 (.in0(4'b0000), .in1(4'b1100), .out(multiplexer_13_out), .sel(SW_type));
  Multiplexer #(.width(4)) multiplexer_14 (.in0(4'b0000), .in1(4'b1101), .out(multiplexer_14_out), .sel(SH_type));
  Multiplexer #(.width(4)) multiplexer_15 (.in0(4'b0000), .in1(4'b1110), .out(multiplexer_15_out), .sel(JAL_type));
  Multiplexer #(.width(4)) multiplexer_16 (.in0(4'b0000), .in1(4'b1111), .out(multiplexer_16_out), .sel(BEQ_type));
  Comparator #(.mode("unsigned"), .width(7)) comparator_3 (
    .a(Inst[6:0]), .b(7'b0110111), .eq(LUI_type));  // open: gt, lt
  Comparator #(.mode("unsigned"), .width(7)) comparator_4 (
    .a(Inst[6:0]), .b(7'b0010111), .eq(AUIPC_type));  // open: gt, lt
  Comparator #(.mode("unsigned"), .width(7)) comparator_5 (
    .a(Inst[6:0]), .b(7'b1101111), .eq(JAL_type));  // open: gt, lt
  Comparator #(.mode("unsigned"), .width(7)) comparator_6 (
    .a(Inst[6:0]), .b(7'b1100111), .eq(JALR_type));  // open: gt, lt
  Comparator #(.mode("unsigned"), .width(7)) comparator_7 (
    .a(Inst[6:0]), .b(7'b1100011), .eq(comparator_7_eq));  // open: gt, lt
  Comparator #(.mode("unsigned"), .width(3)) comparator_8 (
    .a(Inst[14:12]), .b(3'b000), .eq(comparator_8_eq));  // open: gt, lt
  and and_1 (BEQ_type, comparator_7_eq, comparator_8_eq);
  and and_2 (LH_type, comparator_1_eq, comparator_2_eq);
  Multiplexer multiplexer_17 (.in0(1'b0), .in1(1'b0), .out(multiplexer_17_out), .sel(ADD_type));
  Multiplexer multiplexer_18 (.in0(1'b0), .in1(1'b0), .out(multiplexer_18_out), .sel(SRA_type));
  Multiplexer multiplexer_19 (.in0(1'b0), .in1(1'b0), .out(multiplexer_19_out), .sel(SLT_type));
  Multiplexer multiplexer_20 (.in0(1'b0), .in1(1'b0), .out(multiplexer_20_out), .sel(SRLI_type));
  Multiplexer multiplexer_21 (.in0(1'b0), .in1(1'b0), .out(multiplexer_21_out), .sel(SLTIU_type));
  Multiplexer multiplexer_22 (.in0(1'b0), .in1(1'b0), .out(multiplexer_22_out), .sel(ANDI_type));
  Multiplexer multiplexer_23 (.in0(1'b0), .in1(1'b0), .out(multiplexer_23_out), .sel(ADDI_type));
  Multiplexer multiplexer_24 (.in0(1'b0), .in1(1'b0), .out(multiplexer_24_out), .sel(LW_type));
  Multiplexer multiplexer_25 (.in0(1'b0), .in1(1'b0), .out(multiplexer_25_out), .sel(LH_type));
  Multiplexer multiplexer_26 (.in0(1'b0), .in1(1'b1), .out(multiplexer_26_out), .sel(JALR_type));
  Multiplexer multiplexer_27 (.in0(1'b0), .in1(1'b0), .out(multiplexer_27_out), .sel(AUIPC_type));
  Multiplexer multiplexer_28 (.in0(1'b0), .in1(1'b0), .out(multiplexer_28_out), .sel(LUI_type));
  Multiplexer multiplexer_29 (.in0(1'b0), .in1(1'b0), .out(multiplexer_29_out), .sel(SW_type));
  Multiplexer multiplexer_30 (.in0(1'b0), .in1(1'b0), .out(multiplexer_30_out), .sel(SH_type));
  Multiplexer multiplexer_31 (.in0(1'b0), .in1(1'b1), .out(multiplexer_31_out), .sel(JAL_type));
  Multiplexer multiplexer_32 (.in0(1'b0), .in1(1'b1), .out(multiplexer_32_out), .sel(BEQ_type));
  Comparator #(.mode("unsigned"), .width(7)) comparator_9 (
    .a(Inst[6:0]), .b(7'b0000011), .eq(comparator_9_eq));  // open: gt, lt
  Comparator #(.mode("unsigned"), .width(3)) comparator_10 (
    .a(Inst[14:12]), .b(3'b010), .eq(comparator_10_eq));  // open: gt, lt
  Comparator #(.mode("unsigned"), .width(7)) comparator_11 (
    .a(Inst[6:0]), .b(7'b0100011), .eq(comparator_11_eq));  // open: gt, lt
  Comparator #(.mode("unsigned"), .width(3)) comparator_12 (
    .a(Inst[14:12]), .b(3'b010), .eq(comparator_12_eq));  // open: gt, lt
  Comparator #(.mode("unsigned"), .width(7)) comparator_13 (
    .a(Inst[6:0]), .b(7'b0100011), .eq(comparator_13_eq));  // open: gt, lt
  Comparator #(.mode("unsigned"), .width(3)) comparator_14 (
    .a(Inst[14:12]), .b(3'b001), .eq(comparator_14_eq));  // open: gt, lt
  Comparator #(.mode("unsigned"), .width(7)) comparator_15 (
    .a(Inst[6:0]), .b(7'b0010011), .eq(comparator_15_eq));  // open: gt, lt
  Comparator #(.mode("unsigned"), .width(3)) comparator_16 (
    .a(Inst[14:12]), .b(3'b000), .eq(comparator_16_eq));  // open: gt, lt
  Comparator #(.mode("unsigned"), .width(7)) comparator_17 (
    .a(Inst[6:0]), .b(7'b0010011), .eq(comparator_17_eq));  // open: gt, lt
  Comparator #(.mode("unsigned"), .width(3)) comparator_18 (
    .a(Inst[14:12]), .b(3'b011), .eq(comparator_18_eq));  // open: gt, lt
  and and_3 (and_3_out, multiplexer_32_out, Is_equal);
  and and_4 (LW_type, comparator_9_eq, comparator_10_eq);
  and and_5 (SW_type, comparator_11_eq, comparator_12_eq);
  and and_6 (SH_type, comparator_13_eq, comparator_14_eq);
  and and_7 (ADDI_type, comparator_15_eq, comparator_16_eq);
  and and_8 (SLTIU_type, comparator_17_eq, comparator_18_eq);
  Multiplexer multiplexer_33 (.in0(1'b0), .in1(1'b1), .out(multiplexer_33_out), .sel(ADD_type));
  Multiplexer multiplexer_34 (.in0(1'b0), .in1(1'b1), .out(multiplexer_34_out), .sel(SRA_type));
  Multiplexer multiplexer_35 (.in0(1'b0), .in1(1'b1), .out(multiplexer_35_out), .sel(SLT_type));
  Multiplexer multiplexer_36 (.in0(1'b0), .in1(1'b1), .out(multiplexer_36_out), .sel(SRLI_type));
  Multiplexer multiplexer_37 (.in0(1'b0), .in1(1'b1), .out(multiplexer_37_out), .sel(SLTIU_type));
  Multiplexer multiplexer_38 (.in0(1'b0), .in1(1'b1), .out(multiplexer_38_out), .sel(ANDI_type));
  Multiplexer multiplexer_39 (.in0(1'b0), .in1(1'b1), .out(multiplexer_39_out), .sel(ADDI_type));
  Multiplexer multiplexer_40 (.in0(1'b0), .in1(1'b1), .out(multiplexer_40_out), .sel(LW_type));
  Multiplexer multiplexer_41 (.in0(1'b0), .in1(1'b1), .out(multiplexer_41_out), .sel(LH_type));
  Multiplexer multiplexer_42 (.in0(1'b0), .in1(1'b1), .out(multiplexer_42_out), .sel(JALR_type));
  Multiplexer multiplexer_43 (.in0(1'b0), .in1(1'b1), .out(multiplexer_43_out), .sel(AUIPC_type));
  Multiplexer multiplexer_44 (.in0(1'b0), .in1(1'b1), .out(multiplexer_44_out), .sel(LUI_type));
  Multiplexer multiplexer_45 (.in0(1'b0), .in1(1'b0), .out(multiplexer_45_out), .sel(SW_type));
  Multiplexer multiplexer_46 (.in0(1'b0), .in1(1'b0), .out(multiplexer_46_out), .sel(SH_type));
  Multiplexer multiplexer_47 (.in0(1'b0), .in1(1'b1), .out(multiplexer_47_out), .sel(JAL_type));
  Multiplexer multiplexer_48 (.in0(1'b0), .in1(1'b0), .out(multiplexer_48_out), .sel(BEQ_type));
  assign inst_id = multiplexer_1_out | multiplexer_2_out | multiplexer_3_out | multiplexer_4_out | multiplexer_5_out | multiplexer_6_out | multiplexer_7_out | multiplexer_8_out | multiplexer_9_out | multiplexer_10_out | multiplexer_11_out | multiplexer_12_out | multiplexer_13_out | multiplexer_14_out | multiplexer_15_out | multiplexer_16_out;  // OR_Gate or_1, 4 bits wide
  Comparator #(.mode("unsigned"), .width(7)) comparator_19 (
    .a(Inst[6:0]), .b(7'b0010011), .eq(comparator_19_eq));  // open: gt, lt
  Comparator #(.mode("unsigned"), .width(3)) comparator_20 (
    .a(Inst[14:12]), .b(3'b111), .eq(comparator_20_eq));  // open: gt, lt
  Comparator #(.mode("unsigned"), .width(7)) comparator_21 (
    .a(Inst[6:0]), .b(7'b0010011), .eq(comparator_21_eq));  // open: gt, lt
  Comparator #(.mode("unsigned"), .width(3)) comparator_22 (
    .a(Inst[14:12]), .b(3'b101), .eq(comparator_22_eq));  // open: gt, lt
  Comparator #(.mode("unsigned"), .width(7)) comparator_23 (
    .a(Inst[6:0]), .b(7'b0110011), .eq(comparator_23_eq));  // open: gt, lt
  Comparator #(.mode("unsigned"), .width(3)) comparator_24 (
    .a(Inst[14:12]), .b(3'b000), .eq(comparator_24_eq));  // open: gt, lt
  Comparator #(.mode("unsigned"), .width(7)) comparator_25 (
    .a(Inst[6:0]), .b(7'b0110011), .eq(comparator_25_eq));  // open: gt, lt
  Comparator #(.mode("unsigned"), .width(3)) comparator_26 (
    .a(Inst[14:12]), .b(3'b101), .eq(comparator_26_eq));  // open: gt, lt
  Comparator #(.mode("unsigned"), .width(7)) comparator_27 (
    .a(Inst[6:0]), .b(7'b0110011), .eq(comparator_27_eq));  // open: gt, lt
  Comparator #(.mode("unsigned"), .width(3)) comparator_28 (
    .a(Inst[14:12]), .b(3'b010), .eq(comparator_28_eq));  // open: gt, lt
  Multiplexer multiplexer_49 (.in0(1'b0), .in1(1'b0), .out(multiplexer_49_out), .sel(ADD_type));
  Multiplexer multiplexer_50 (.in0(1'b0), .in1(1'b0), .out(multiplexer_50_out), .sel(SRA_type));
  Multiplexer multiplexer_51 (.in0(1'b0), .in1(1'b0), .out(multiplexer_51_out), .sel(SLT_type));
  Multiplexer multiplexer_52 (.in0(1'b0), .in1(1'b0), .out(multiplexer_52_out), .sel(SRLI_type));
  Multiplexer multiplexer_53 (.in0(1'b0), .in1(1'b0), .out(multiplexer_53_out), .sel(SLTIU_type));
  Multiplexer multiplexer_54 (.in0(1'b0), .in1(1'b0), .out(multiplexer_54_out), .sel(ANDI_type));
  Multiplexer multiplexer_55 (.in0(1'b0), .in1(1'b0), .out(multiplexer_55_out), .sel(ADDI_type));
  Multiplexer multiplexer_56 (.in0(1'b0), .in1(1'b0), .out(multiplexer_56_out), .sel(LW_type));
  Multiplexer multiplexer_57 (.in0(1'b0), .in1(1'b0), .out(multiplexer_57_out), .sel(LH_type));
  Multiplexer multiplexer_58 (.in0(1'b0), .in1(1'b0), .out(multiplexer_58_out), .sel(JALR_type));
  Multiplexer multiplexer_59 (.in0(1'b0), .in1(1'b0), .out(multiplexer_59_out), .sel(AUIPC_type));
  Multiplexer multiplexer_60 (.in0(1'b0), .in1(1'b0), .out(multiplexer_60_out), .sel(LUI_type));
  Multiplexer multiplexer_61 (.in0(1'b0), .in1(1'b1), .out(multiplexer_61_out), .sel(SW_type));
  Multiplexer multiplexer_62 (.in0(1'b0), .in1(1'b1), .out(multiplexer_62_out), .sel(SH_type));
  Multiplexer multiplexer_63 (.in0(1'b0), .in1(1'b0), .out(multiplexer_63_out), .sel(JAL_type));
  Multiplexer multiplexer_64 (.in0(1'b0), .in1(1'b0), .out(multiplexer_64_out), .sel(BEQ_type));
  or or_2 (PCsel, multiplexer_17_out, multiplexer_18_out, multiplexer_19_out, multiplexer_20_out, multiplexer_21_out, multiplexer_22_out, multiplexer_23_out, multiplexer_24_out, multiplexer_25_out, multiplexer_26_out, multiplexer_27_out, multiplexer_28_out, multiplexer_29_out, multiplexer_30_out, multiplexer_31_out, and_3_out);
  and and_9 (ANDI_type, comparator_19_eq, comparator_20_eq);
  and and_10 (SRLI_type, comparator_21_eq, comparator_22_eq);
  and and_11 (ADD_type, comparator_23_eq, comparator_24_eq);
  and and_12 (SRA_type, comparator_25_eq, comparator_26_eq);
  and and_13 (SLT_type, comparator_27_eq, comparator_28_eq);
  Multiplexer multiplexer_65 (.in0(1'b0), .in1(1'b0), .out(multiplexer_65_out), .sel(ADD_type));
  Multiplexer multiplexer_66 (.in0(1'b0), .in1(1'b0), .out(multiplexer_66_out), .sel(SRA_type));
  Multiplexer multiplexer_67 (.in0(1'b0), .in1(1'b0), .out(multiplexer_67_out), .sel(SLT_type));
  Multiplexer multiplexer_68 (.in0(1'b0), .in1(1'b0), .out(multiplexer_68_out), .sel(SRLI_type));
  Multiplexer multiplexer_69 (.in0(1'b0), .in1(1'b0), .out(multiplexer_69_out), .sel(SLTIU_type));
  Multiplexer multiplexer_70 (.in0(1'b0), .in1(1'b0), .out(multiplexer_70_out), .sel(ANDI_type));
  Multiplexer multiplexer_71 (.in0(1'b0), .in1(1'b0), .out(multiplexer_71_out), .sel(ADDI_type));
  Multiplexer multiplexer_72 (.in0(1'b0), .in1(1'b0), .out(multiplexer_72_out), .sel(LW_type));
  Multiplexer multiplexer_73 (.in0(1'b0), .in1(1'b0), .out(multiplexer_73_out), .sel(LH_type));
  Multiplexer multiplexer_74 (.in0(1'b0), .in1(1'b0), .out(multiplexer_74_out), .sel(JALR_type));
  Multiplexer multiplexer_75 (.in0(1'b0), .in1(1'b0), .out(multiplexer_75_out), .sel(AUIPC_type));
  Multiplexer multiplexer_76 (.in0(1'b0), .in1(1'b0), .out(multiplexer_76_out), .sel(LUI_type));
  Multiplexer multiplexer_77 (.in0(1'b0), .in1(1'b0), .out(multiplexer_77_out), .sel(SW_type));
  Multiplexer multiplexer_78 (.in0(1'b0), .in1(1'b1), .out(multiplexer_78_out), .sel(SH_type));
  Multiplexer multiplexer_79 (.in0(1'b0), .in1(1'b0), .out(multiplexer_79_out), .sel(JAL_type));
  Multiplexer multiplexer_80 (.in0(1'b0), .in1(1'b0), .out(multiplexer_80_out), .sel(BEQ_type));
  or or_3 (RegWEn, multiplexer_33_out, multiplexer_34_out, multiplexer_35_out, multiplexer_36_out, multiplexer_37_out, multiplexer_38_out, multiplexer_39_out, multiplexer_40_out, multiplexer_41_out, multiplexer_42_out, multiplexer_43_out, multiplexer_44_out, multiplexer_45_out, multiplexer_46_out, multiplexer_47_out, multiplexer_48_out);
  Multiplexer multiplexer_81 (.in0(1'b0), .in1(1'b0), .out(multiplexer_81_out), .sel(ADD_type));
  Multiplexer multiplexer_82 (.in0(1'b0), .in1(1'b0), .out(multiplexer_82_out), .sel(SRA_type));
  Multiplexer multiplexer_83 (.in0(1'b0), .in1(1'b0), .out(multiplexer_83_out), .sel(SLT_type));
  Multiplexer multiplexer_84 (.in0(1'b0), .in1(1'b0), .out(multiplexer_84_out), .sel(SRLI_type));
  Multiplexer multiplexer_85 (.in0(1'b0), .in1(1'b0), .out(multiplexer_85_out), .sel(SLTIU_type));
  Multiplexer multiplexer_86 (.in0(1'b0), .in1(1'b0), .out(multiplexer_86_out), .sel(ANDI_type));
  Multiplexer multiplexer_87 (.in0(1'b0), .in1(1'b0), .out(multiplexer_87_out), .sel(ADDI_type));
  Multiplexer multiplexer_88 (.in0(1'b0), .in1(1'b0), .out(multiplexer_88_out), .sel(LW_type));
  Multiplexer multiplexer_89 (.in0(1'b0), .in1(1'b1), .out(multiplexer_89_out), .sel(LH_type));
  Multiplexer multiplexer_90 (.in0(1'b0), .in1(1'b0), .out(multiplexer_90_out), .sel(JALR_type));
  Multiplexer multiplexer_91 (.in0(1'b0), .in1(1'b0), .out(multiplexer_91_out), .sel(AUIPC_type));
  Multiplexer multiplexer_92 (.in0(1'b0), .in1(1'b0), .out(multiplexer_92_out), .sel(LUI_type));
  Multiplexer multiplexer_93 (.in0(1'b0), .in1(1'b0), .out(multiplexer_93_out), .sel(SW_type));
  Multiplexer multiplexer_94 (.in0(1'b0), .in1(1'b0), .out(multiplexer_94_out), .sel(SH_type));
  Multiplexer multiplexer_95 (.in0(1'b0), .in1(1'b0), .out(multiplexer_95_out), .sel(JAL_type));
  Multiplexer multiplexer_96 (.in0(1'b0), .in1(1'b0), .out(multiplexer_96_out), .sel(BEQ_type));
  or or_4 (MemRW, multiplexer_49_out, multiplexer_50_out, multiplexer_51_out, multiplexer_52_out, multiplexer_53_out, multiplexer_54_out, multiplexer_55_out, multiplexer_56_out, multiplexer_57_out, multiplexer_58_out, multiplexer_59_out, multiplexer_60_out, multiplexer_61_out, multiplexer_62_out, multiplexer_63_out, multiplexer_64_out);
  Multiplexer multiplexer_97 (.in0(1'b0), .in1(1'b1), .out(multiplexer_97_out), .sel(ADD_type));
  Multiplexer multiplexer_98 (.in0(1'b0), .in1(1'b1), .out(multiplexer_98_out), .sel(SRA_type));
  Multiplexer multiplexer_99 (.in0(1'b0), .in1(1'b1), .out(multiplexer_99_out), .sel(SLT_type));
  Multiplexer multiplexer_100 (.in0(1'b0), .in1(1'b1), .out(multiplexer_100_out), .sel(SRLI_type));
  Multiplexer multiplexer_101 (.in0(1'b0), .in1(1'b1), .out(multiplexer_101_out), .sel(SLTIU_type));
  Multiplexer multiplexer_102 (.in0(1'b0), .in1(1'b1), .out(multiplexer_102_out), .sel(ANDI_type));
  Multiplexer multiplexer_103 (.in0(1'b0), .in1(1'b1), .out(multiplexer_103_out), .sel(ADDI_type));
  Multiplexer multiplexer_104 (.in0(1'b0), .in1(1'b0), .out(multiplexer_104_out), .sel(LW_type));
  Multiplexer multiplexer_105 (.in0(1'b0), .in1(1'b0), .out(multiplexer_105_out), .sel(LH_type));
  Multiplexer multiplexer_106 (.in0(1'b0), .in1(1'b1), .out(multiplexer_106_out), .sel(JALR_type));
  Multiplexer multiplexer_107 (.in0(1'b0), .in1(1'b1), .out(multiplexer_107_out), .sel(AUIPC_type));
  Multiplexer multiplexer_108 (.in0(1'b0), .in1(1'b1), .out(multiplexer_108_out), .sel(LUI_type));
  Multiplexer multiplexer_109 (.in0(1'b0), .in1(1'b1), .out(multiplexer_109_out), .sel(SW_type));
  Multiplexer multiplexer_110 (.in0(1'b0), .in1(1'b1), .out(multiplexer_110_out), .sel(SH_type));
  Multiplexer multiplexer_111 (.in0(1'b0), .in1(1'b1), .out(multiplexer_111_out), .sel(JAL_type));
  Multiplexer multiplexer_112 (.in0(1'b0), .in1(1'b1), .out(multiplexer_112_out), .sel(BEQ_type));
  or or_5 (Write_half, multiplexer_65_out, multiplexer_66_out, multiplexer_67_out, multiplexer_68_out, multiplexer_69_out, multiplexer_70_out, multiplexer_71_out, multiplexer_72_out, multiplexer_73_out, multiplexer_74_out, multiplexer_75_out, multiplexer_76_out, multiplexer_77_out, multiplexer_78_out, multiplexer_79_out, multiplexer_80_out);
  or or_6 (Read_half, multiplexer_81_out, multiplexer_82_out, multiplexer_83_out, multiplexer_84_out, multiplexer_85_out, multiplexer_86_out, multiplexer_87_out, multiplexer_88_out, multiplexer_89_out, multiplexer_90_out, multiplexer_91_out, multiplexer_92_out, multiplexer_93_out, multiplexer_94_out, multiplexer_95_out, multiplexer_96_out);
  or or_7 (WB_sel, multiplexer_97_out, multiplexer_98_out, multiplexer_99_out, multiplexer_100_out, multiplexer_101_out, multiplexer_102_out, multiplexer_103_out, multiplexer_104_out, multiplexer_105_out, multiplexer_106_out, multiplexer_107_out, multiplexer_108_out, multiplexer_109_out, multiplexer_110_out, multiplexer_111_out, multiplexer_112_out);

  // Other names for the same wires on the sheet: Opcode[6:0] = Inst[6:0]; Func3[2:0] = Inst[14:12]
endmodule

module Data_Hazard_logic_A (
  input  [31:0] Inst_now,
  input  [3:0] Inst_id_now,
  input  [31:0] Inst_last_1,
  input  [3:0] Inst_id_last_1,
  input  [31:0] Inst_last_2,
  input  [3:0] Inst_id_last_2,
  output [1:0] Data_Hazard_choice
);

  wire and_1_out, and_2_out, and_4_out, and_5_out, and_6_out, and_7_out, comparator_1_eq, comparator_2_eq,
       comparator_3_eq, comparator_4_eq, comparator_5_eq, comparator_6_eq, comparator_7_eq, comparator_8_eq,
       comparator_9_eq, comparator_10_eq, comparator_11_eq, comparator_12_eq, comparator_13_eq,
       comparator_14_eq, Data_hazard_0, Data_hazard_1, Data_hazard_2, Have_RD_1, Have_RD_2, Need_RS1,
       not_1_out, not_2_out, not_3_out, not_4_out, not_5_out, not_9_out, or_1_out, or_2_out, or_3_out;
  wire [1:0] multiplexer_1_out, multiplexer_2_out, multiplexer_3_out;

  Comparator #(.width(5)) comparator_1 (
    .a(Inst_last_1[11:7]), .b(Inst_now[19:15]), .eq(comparator_1_eq));  // open: gt, lt
  Comparator #(.width(5)) comparator_2 (
    .a(Inst_last_2[11:7]), .b(Inst_now[19:15]), .eq(comparator_2_eq));  // open: gt, lt
  Comparator #(.width(4)) comparator_3 (.a(4'b1010), .b(Inst_id_now), .eq(comparator_3_eq));  // open: gt, lt
  Comparator #(.width(4)) comparator_4 (.a(4'b1011), .b(Inst_id_now), .eq(comparator_4_eq));  // open: gt, lt
  Comparator #(.width(4)) comparator_5 (.a(Inst_id_now), .b(4'b1110), .eq(comparator_5_eq));  // open: gt, lt
  Comparator #(.width(4)) comparator_6 (.a(4'b1100), .b(Inst_id_last_1), .eq(comparator_6_eq));  // open: gt, lt
  Comparator #(.width(4)) comparator_7 (.a(4'b1101), .b(Inst_id_last_1), .eq(comparator_7_eq));  // open: gt, lt
  Comparator #(.width(4)) comparator_8 (.a(Inst_id_last_1), .b(4'b1111), .eq(comparator_8_eq));  // open: gt, lt
  Comparator #(.width(4)) comparator_9 (.a(4'b1100), .b(Inst_id_last_2), .eq(comparator_9_eq));  // open: gt, lt
  Comparator #(.width(4)) comparator_10 (.a(4'b1101), .b(Inst_id_last_2), .eq(comparator_10_eq));  // open: gt, lt
  Comparator #(.width(4)) comparator_11 (.a(Inst_id_last_2), .b(4'b1111), .eq(comparator_11_eq));  // open: gt, lt
  Comparator #(.width(5)) comparator_12 (
    .a(Inst_last_1[11:7]), .b(Inst_now[19:15]), .eq(comparator_12_eq));  // open: gt, lt
  and and_1 (and_1_out, Need_RS1, Have_RD_1, comparator_1_eq);
  and and_2 (and_2_out, Need_RS1, Have_RD_2, comparator_2_eq);
  Comparator #(.width(5)) comparator_13 (
    .a(Inst_last_1[11:7]), .b(Inst_now[19:15]), .eq(comparator_13_eq));  // open: gt, lt
  Comparator #(.width(5)) comparator_14 (
    .a(Inst_last_2[11:7]), .b(Inst_now[19:15]), .eq(comparator_14_eq));  // open: gt, lt
  or or_1 (or_1_out, comparator_3_eq, comparator_4_eq, comparator_5_eq);
  or or_2 (or_2_out, comparator_6_eq, comparator_7_eq, comparator_8_eq);
  or or_3 (or_3_out, comparator_9_eq, comparator_10_eq, comparator_11_eq);
  not not_1 (not_1_out, Need_RS1);
  not not_2 (not_2_out, Have_RD_1);
  not not_3 (not_3_out, Have_RD_2);
  not not_4 (not_4_out, and_1_out);
  not not_5 (not_5_out, and_2_out);
  and and_3 (Data_hazard_1, Need_RS1, Have_RD_1, comparator_12_eq);
  and and_4 (and_4_out, Need_RS1, Have_RD_1, comparator_13_eq);
  not not_6 (Need_RS1, or_1_out);
  not not_7 (Have_RD_1, or_2_out);
  not not_8 (Have_RD_2, or_3_out);
  and and_5 (and_5_out, not_2_out, not_3_out);
  and and_6 (and_6_out, not_4_out, not_5_out);
  and and_7 (and_7_out, Need_RS1, Have_RD_2, comparator_14_eq);
  not not_9 (not_9_out, and_4_out);
  and and_8 (Data_hazard_2, not_9_out, and_7_out);
  or or_4 (Data_hazard_0, not_1_out, and_5_out, and_6_out);
  Multiplexer #(.width(2)) multiplexer_1 (.in0(2'b00), .in1(2'b00), .out(multiplexer_1_out), .sel(Data_hazard_0));
  Multiplexer #(.width(2)) multiplexer_2 (.in0(2'b00), .in1(2'b01), .out(multiplexer_2_out), .sel(Data_hazard_1));
  Multiplexer #(.width(2)) multiplexer_3 (.in0(2'b00), .in1(2'b10), .out(multiplexer_3_out), .sel(Data_hazard_2));
  assign Data_Hazard_choice = multiplexer_1_out | multiplexer_2_out | multiplexer_3_out;  // OR_Gate or_5, 2 bits wide

  // Other names for the same wires on the sheet: Data_Hazard[1:0] = Data_Hazard_choice; RD_1[4:0] = Inst_last_1[11:7];
  //   RD_2[4:0] = Inst_last_2[11:7]; RS1_now[4:0] = Inst_now[19:15]
endmodule

module Data_Hazard_logic_B (
  input  [31:0] Inst_now,
  input  [3:0] Inst_id_now,
  input  [31:0] Inst_last_1,
  input  [3:0] Inst_id_last_1,
  input  [31:0] Inst_last_2,
  input  [3:0] Inst_id_last_2,
  output [1:0] Data_Hazard_choice
);

  wire and_1_out, and_2_out, and_4_out, and_5_out, and_6_out, and_7_out, comparator_1_eq, comparator_2_eq,
       comparator_3_eq, comparator_4_eq, comparator_5_eq, comparator_6_eq, comparator_7_eq, comparator_8_eq,
       comparator_9_eq, comparator_10_eq, comparator_11_eq, comparator_12_eq, comparator_13_eq,
       comparator_14_eq, comparator_15_eq, comparator_16_eq, comparator_17_eq, Data_hazard_0, Data_hazard_1,
       Data_hazard_2, Have_RD_1, Have_RD_2, Need_RS2, not_1_out, not_2_out, not_3_out, not_4_out, not_5_out,
       not_8_out, or_1_out, or_2_out;
  wire [1:0] multiplexer_1_out, multiplexer_2_out, multiplexer_3_out;

  Comparator #(.width(5)) comparator_1 (
    .a(Inst_last_1[11:7]), .b(Inst_now[24:20]), .eq(comparator_1_eq));  // open: gt, lt
  Comparator #(.width(5)) comparator_2 (
    .a(Inst_last_2[11:7]), .b(Inst_now[24:20]), .eq(comparator_2_eq));  // open: gt, lt
  Comparator #(.width(4)) comparator_3 (.a(4'b0000), .b(Inst_id_now), .eq(comparator_3_eq));  // open: gt, lt
  Comparator #(.width(4)) comparator_4 (.a(4'b0001), .b(Inst_id_now), .eq(comparator_4_eq));  // open: gt, lt
  Comparator #(.width(4)) comparator_5 (.a(4'b0010), .b(Inst_id_now), .eq(comparator_5_eq));  // open: gt, lt
  Comparator #(.width(4)) comparator_6 (.a(4'b1100), .b(Inst_id_now), .eq(comparator_6_eq));  // open: gt, lt
  Comparator #(.width(4)) comparator_7 (.a(Inst_id_now), .b(4'b1101), .eq(comparator_7_eq));  // open: gt, lt
  Comparator #(.width(4)) comparator_8 (.a(4'b1111), .b(Inst_id_now), .eq(comparator_8_eq));  // open: gt, lt
  Comparator #(.width(4)) comparator_9 (.a(4'b1100), .b(Inst_id_last_1), .eq(comparator_9_eq));  // open: gt, lt
  Comparator #(.width(4)) comparator_10 (.a(4'b1101), .b(Inst_id_last_1), .eq(comparator_10_eq));  // open: gt, lt
  Comparator #(.width(4)) comparator_11 (.a(Inst_id_last_1), .b(4'b1111), .eq(comparator_11_eq));  // open: gt, lt
  Comparator #(.width(4)) comparator_12 (.a(4'b1100), .b(Inst_id_last_2), .eq(comparator_12_eq));  // open: gt, lt
  Comparator #(.width(4)) comparator_13 (.a(4'b1101), .b(Inst_id_last_2), .eq(comparator_13_eq));  // open: gt, lt
  Comparator #(.width(4)) comparator_14 (.a(Inst_id_last_2), .b(4'b1111), .eq(comparator_14_eq));  // open: gt, lt
  Comparator #(.width(5)) comparator_15 (
    .a(Inst_last_1[11:7]), .b(Inst_now[24:20]), .eq(comparator_15_eq));  // open: gt, lt
  and and_1 (and_1_out, Need_RS2, Have_RD_1, comparator_1_eq);
  and and_2 (and_2_out, Need_RS2, Have_RD_2, comparator_2_eq);
  Comparator #(.width(5)) comparator_16 (
    .a(Inst_last_1[11:7]), .b(Inst_now[24:20]), .eq(comparator_16_eq));  // open: gt, lt
  Comparator #(.width(5)) comparator_17 (
    .a(Inst_last_2[11:7]), .b(Inst_now[24:20]), .eq(comparator_17_eq));  // open: gt, lt
  or or_1 (or_1_out, comparator_9_eq, comparator_10_eq, comparator_11_eq);
  or or_2 (or_2_out, comparator_12_eq, comparator_13_eq, comparator_14_eq);
  not not_1 (not_1_out, Need_RS2);
  not not_2 (not_2_out, Have_RD_1);
  not not_3 (not_3_out, Have_RD_2);
  not not_4 (not_4_out, and_1_out);
  not not_5 (not_5_out, and_2_out);
  and and_3 (Data_hazard_1, Need_RS2, Have_RD_1, comparator_15_eq);
  and and_4 (and_4_out, Need_RS2, Have_RD_1, comparator_16_eq);
  or or_3 (Need_RS2, comparator_3_eq, comparator_4_eq, comparator_5_eq, comparator_6_eq, comparator_7_eq, comparator_8_eq);
  not not_6 (Have_RD_1, or_1_out);
  not not_7 (Have_RD_2, or_2_out);
  and and_5 (and_5_out, not_2_out, not_3_out);
  and and_6 (and_6_out, not_4_out, not_5_out);
  and and_7 (and_7_out, Need_RS2, Have_RD_2, comparator_17_eq);
  not not_8 (not_8_out, and_4_out);
  and and_8 (Data_hazard_2, not_8_out, and_7_out);
  or or_4 (Data_hazard_0, not_1_out, and_5_out, and_6_out);
  Multiplexer #(.width(2)) multiplexer_1 (.in0(2'b00), .in1(2'b00), .out(multiplexer_1_out), .sel(Data_hazard_0));
  Multiplexer #(.width(2)) multiplexer_2 (.in0(2'b00), .in1(2'b01), .out(multiplexer_2_out), .sel(Data_hazard_1));
  Multiplexer #(.width(2)) multiplexer_3 (.in0(2'b00), .in1(2'b10), .out(multiplexer_3_out), .sel(Data_hazard_2));
  assign Data_Hazard_choice = multiplexer_1_out | multiplexer_2_out | multiplexer_3_out;  // OR_Gate or_5, 2 bits wide

  // Other names for the same wires on the sheet: Data_Hazard[1:0] = Data_Hazard_choice; RD_1[4:0] = Inst_last_1[11:7];
  //   RD_2[4:0] = Inst_last_2[11:7]; RS2_now[4:0] = Inst_now[24:20]
endmodule

module Control_Hazard_logic (
  input  Jump,
  output Control_Hazard
);


  assign Control_Hazard = Jump;
endmodule
